// Logisim project Cordic_Examples.circ as structural Verilog
module Cordic_16_Bits_Input (
  input  [15:0] z_0,
  input  in_2
);

  wire clk, DFF_out, msb, not_1_out, not_2_out;
  wire [3:0] cnt, counter_1_q;
  wire [14:0] z_i_1;
  wire [15:0] arc_tan_table, multiplexer_1_out, multiplexer_2_out, multiplexer_3_out, multiplexer_4_out,
       register_2_q, register_3_q, register_4_q, x_i1, x_i_shifted, y_i1, y_i_shifted;

  Clock clock_1 (.out(clk));
  D_Flip_Flop d_ff_1 (.clk(clk), .D(1'b1), .Q(DFF_out), .reset(in_2));  // open: Qn, preset, en
  Multiplexer #(.select(4), .width(16), .enable("false")) multiplexer_1 (
    .in0({16{1'b0}}), .in1(16'h2000), .in2(16'h12e4), .in3(16'h9fb), .in4(16'h511), .in5(16'h28b),
    .in6(16'h146), .in7(16'ha3), .in8(16'h51), .in9(16'h29), .in10(16'h14), .in11(16'ha), .in12(16'h5),
    .in13(16'h3), .in14(16'h2), .in15(16'h1), .out(multiplexer_1_out), .sel(counter_1_q));
  Counter #(.width(4), .max('hf), .ongoal("stay")) counter_1 (
    .Q(counter_1_q), .clk(clk), .clr(in_2));  // open: load, D, count, carry
  Register #(.width(16)) register_1 (.D(multiplexer_1_out), .Q(arc_tan_table), .clk(clk), .clr(in_2));  // open: en
  Subtractor #(.width(4)) subtractor_1 (.a(counter_1_q), .b(4'b0001), .out(cnt));  // open: bin, bout
  Multiplexer #(.width(16), .enable("false")) multiplexer_2 (
    .in0(16'h4dba), .in1(x_i1), .out(multiplexer_2_out), .sel(DFF_out));
  Multiplexer #(.width(16), .enable("false")) multiplexer_3 (
    .in0(16'h2fdc), .in1({msb, z_i_1}), .out(multiplexer_3_out), .sel(DFF_out));
  Register #(.width(16)) register_2 (.D(multiplexer_2_out), .Q(register_2_q), .clk(clk), .clr(in_2));  // open: en
  Register #(.width(16)) register_3 (.D(multiplexer_3_out), .Q(register_3_q), .clk(clk), .clr(in_2));  // open: en
  Shift_Right Shifter (.A(register_2_q), .Select(cnt), .A_Shifted(x_i_shifted));
  Multiplexer #(.width(16), .enable("false")) multiplexer_4 (
    .in0({16{1'b0}}), .in1(y_i1), .out(multiplexer_4_out), .sel(DFF_out));
  Register #(.width(16)) register_4 (.D(multiplexer_4_out), .Q(register_4_q), .clk(clk), .clr(in_2));  // open: en
  _16_Bits_Ripple_Carry_Adder u_16_bits_ripple_carry_adder_1 (
    .A(register_3_q), .B(arc_tan_table), .C_in(not_1_out), .Sum({msb, z_i_1}));  // open: MSB, C_out
  not not_1 (not_1_out, register_3_q[15]);
  // Probe on {msb, z_i_1}
  // Probe on x_i1
  _16_Bits_Ripple_Carry_Adder u_16_bits_ripple_carry_adder_2 (
    .A(register_2_q), .B(y_i_shifted), .C_in(not_2_out), .Sum(x_i1));  // open: MSB, C_out
  not not_2 (not_2_out, msb);
  Shift_Right shift_right_1 (.A(register_4_q), .Select(cnt), .A_Shifted(y_i_shifted));
  // Probe on y_i1
  _16_Bits_Ripple_Carry_Adder u_16_bits_ripple_carry_adder_3 (
    .A(register_4_q), .B(x_i_shifted), .C_in(msb), .Sum(y_i1));  // open: MSB, C_out

  // Other names for the same wires on the sheet: RESET = in_2; z_i_1[15] = msb

  // Notes on the sheet:
  //   Toggle clock to calculate
endmodule

module Cordic_32_Bits_Input (
  input  [31:0] z_0,
  input  in_2
);

  wire clk, d_ff_1_q, d_ff_2_q, d_ff_3_q, MSB, MSB2, MSB3, not_1_out, not_2_out;
  wire [3:0] COUNTER, counter_1_q;
  wire [30:0] multiplexer_2_out, register_2_q, z_i_1;
  wire [31:0] arc_tan_table, multiplexer_1_out, multiplexer_3_out, multiplexer_4_out, register_3_q,
       register_4_q, x_i1, x_i_shifted, y_i_1, y_i_shifted;

  Clock clock_1 (.out(clk));
  Subtractor #(.width(4)) subtractor_1 (.a(counter_1_q), .b(4'b0001), .out(COUNTER));  // open: bin, bout
  Counter #(.width(4), .max('hf), .ongoal("stay")) counter_1 (
    .Q(counter_1_q), .clk(clk), .clr(in_2));  // open: load, D, count, carry
  D_Flip_Flop d_ff_1 (.clk(clk), .D(1'b1), .Q(d_ff_1_q), .reset(in_2));  // open: Qn, preset, en
  Multiplexer #(.select(4), .width(32), .enable("false")) multiplexer_1 (
    .in0({32{1'b0}}), .in1(32'h20000000), .in2(32'h12e4051e), .in3(32'h9fb385b), .in4(32'h51111d4),
    .in5(32'h28b0d43), .in6(32'h145d7e1), .in7(32'ha2f61e), .in8(32'h517c55), .in9(32'h28be53),
    .in10(32'h145f2f), .in11(32'ha2f98), .in12(32'h517cc), .in13(32'h28be6), .in14(32'h145f3),
    .in15(32'ha2fa), .out(multiplexer_1_out), .sel(counter_1_q));
  // Probe on multiplexer_1_out
  Multiplexer #(.width(32), .enable("false")) multiplexer_2 (
    .in0(32'h2fdb9753), .in1({MSB3, z_i_1}), .out({MSB2, multiplexer_2_out}), .sel(d_ff_1_q));
  // Probe on {MSB2, multiplexer_2_out}
  D_Flip_Flop d_ff_2 (.clk(clk), .D(1'b1), .Q(d_ff_2_q), .reset(in_2));  // open: Qn, preset, en
  Register #(.width(32)) register_1 (.D(multiplexer_1_out), .Q(arc_tan_table), .clk(clk), .clr(in_2));  // open: en
  Register #(.width(32)) register_2 (
    .D({MSB2, multiplexer_2_out}), .Q({MSB, register_2_q}), .clk(clk), .clr(in_2));  // open: en
  Multiplexer #(.width(32), .enable("false")) multiplexer_3 (
    .in0(32'h4dba76d5), .in1(x_i1), .out(multiplexer_3_out), .sel(d_ff_2_q));
  // Probe on multiplexer_3_out
  Multiplexer #(.width(32), .enable("false")) multiplexer_4 (
    .in0({32{1'b0}}), .in1(y_i_1), .out(multiplexer_4_out), .sel(d_ff_3_q));
  D_Flip_Flop d_ff_3 (.clk(clk), .D(1'b1), .Q(d_ff_3_q), .reset(in_2));  // open: Qn, preset, en
  // Probe on multiplexer_4_out
  Register #(.width(32)) register_3 (.D(multiplexer_3_out), .Q(register_3_q), .clk(clk), .clr(in_2));  // open: en
  Register #(.width(32)) register_4 (.D(multiplexer_4_out), .Q(register_4_q), .clk(clk), .clr(in_2));  // open: en
  not not_1 (not_1_out, MSB);
  _32_Bits_Ripple_Carry_Adder ADD_SUB (
    .A({MSB, register_2_q}), .B(arc_tan_table), .C_in(not_1_out), .SUM({MSB3, z_i_1}));  // open: MSB
  // Probe on {MSB3, z_i_1}
  Shifter #(.width(32), .shift("ar")) shifter_1 (.in(register_3_q), .\dist ({1'b0, COUNTER}), .out(x_i_shifted));
  Shifter #(.width(32), .shift("ar")) shifter_2 (.in(register_4_q), .\dist ({1'b0, COUNTER}), .out(y_i_shifted));
  // Probe on {MSB, register_2_q}
  not not_2 (not_2_out, MSB3);
  // Probe on x_i1
  _32_Bits_Ripple_Carry_Adder ADD_SUB_2 (.A(register_3_q), .B(y_i_shifted), .C_in(not_2_out), .SUM(x_i1));  // open: MSB
  _32_Bits_Ripple_Carry_Adder ADD_SUB_3 (.A(register_4_q), .B(x_i_shifted), .C_in(MSB3), .SUM(y_i_1));  // open: MSB
  // Probe on y_i_1

  // Other names for the same wires on the sheet: RESET = in_2; z_i_1[31] = MSB3

  // Notes on the sheet:
  //   Toggle clock to calculate
endmodule

module _1_Bit_Full_Adder (
  input  A,
  input  B,
  input  C_in,
  output S,
  output C_out
);

  wire and_1_out, and_2_out, xor_1_out;

  xor xor_1 (xor_1_out, A, B);
  xor xor_2 (S, C_in, xor_1_out);
  and and_1 (and_1_out, xor_1_out, C_in);
  and and_2 (and_2_out, A, B);
  or or_1 (C_out, and_1_out, and_2_out);
endmodule

module _8_Bits_Ripple_Carry_Adder (
  input  [7:0] A,
  input  [7:0] B,
  input  C_in,
  output [7:0] A_B,
  output C_out
);

  wire n1_bit_full_adder_1_c_out, n1_bit_full_adder_2_c_out, n1_bit_full_adder_3_c_out,
       n1_bit_full_adder_4_c_out, n1_bit_full_adder_5_c_out, n1_bit_full_adder_6_c_out,
       n1_bit_full_adder_7_c_out;

  _1_Bit_Full_Adder u_1_bit_full_adder_1 (
    .A(A[0]), .B(B[0]), .C_in(C_in), .S(A_B[0]), .C_out(n1_bit_full_adder_1_c_out));
  _1_Bit_Full_Adder u_1_bit_full_adder_2 (
    .A(A[1]), .B(B[1]), .C_in(n1_bit_full_adder_1_c_out), .S(A_B[1]), .C_out(n1_bit_full_adder_2_c_out));
  _1_Bit_Full_Adder u_1_bit_full_adder_3 (
    .A(A[2]), .B(B[2]), .C_in(n1_bit_full_adder_2_c_out), .S(A_B[2]), .C_out(n1_bit_full_adder_3_c_out));
  _1_Bit_Full_Adder u_1_bit_full_adder_4 (
    .A(A[3]), .B(B[3]), .C_in(n1_bit_full_adder_3_c_out), .S(A_B[3]), .C_out(n1_bit_full_adder_4_c_out));
  _1_Bit_Full_Adder u_1_bit_full_adder_5 (
    .A(A[4]), .B(B[4]), .C_in(n1_bit_full_adder_4_c_out), .S(A_B[4]), .C_out(n1_bit_full_adder_5_c_out));
  _1_Bit_Full_Adder u_1_bit_full_adder_6 (
    .A(A[5]), .B(B[5]), .C_in(n1_bit_full_adder_5_c_out), .S(A_B[5]), .C_out(n1_bit_full_adder_6_c_out));
  _1_Bit_Full_Adder u_1_bit_full_adder_7 (
    .A(A[6]), .B(B[6]), .C_in(n1_bit_full_adder_6_c_out), .S(A_B[6]), .C_out(n1_bit_full_adder_7_c_out));
  _1_Bit_Full_Adder u_1_bit_full_adder_8 (
    .A(A[7]), .B(B[7]), .C_in(n1_bit_full_adder_7_c_out), .S(A_B[7]), .C_out(C_out));

  // Other names for the same wires on the sheet: Y0 = A_B[0]; Y1 = A_B[1]; Y2 = A_B[2]; Y3 = A_B[3]; Y4 = A_B[4];
  //   Y5 = A_B[5]; Y6 = A_B[6]; Y7 = A_B[7]
endmodule

module _16_Bits_Ripple_Carry_Adder (
  input  [15:0] A,
  input  [15:0] B,
  input  C_in,
  output [15:0] Sum,
  output MSB,
  output C_out
);

  wire multiplexer_2_out, n8_bits_ripple_carry_adder_1_c_out;
  wire [7:0] B1, B2;
  wire [15:0] not_1_out;

  // Probe on A
  // Probe on B
  Multiplexer #(.width(16), .enable("false")) multiplexer_1 (.in0(B), .in1(not_1_out), .out({B2, B1}), .sel(C_in));
  assign not_1_out = ~B;  // NOT_Gate not_1, 16 bits wide
  _8_Bits_Ripple_Carry_Adder u_8_bits_ripple_carry_adder_1 (
    .A(A[7:0]), .B(B1), .C_in(multiplexer_2_out), .A_B(Sum[7:0]), .C_out(n8_bits_ripple_carry_adder_1_c_out));
  Multiplexer #(.enable("false")) multiplexer_2 (.in0(1'b0), .in1(1'b1), .out(multiplexer_2_out), .sel(C_in));
  _8_Bits_Ripple_Carry_Adder u_8_bits_ripple_carry_adder_2 (
    .A(A[15:8]), .B(B2), .C_in(n8_bits_ripple_carry_adder_1_c_out), .A_B({MSB, Sum[14:8]}), .C_out(C_out));
  // Probe on {MSB, Sum[14:0]}

  assign Sum[15] = MSB;

  // Other names for the same wires on the sheet: A1[7:0] = A[7:0]; A2[7:0] = A[15:8]; ADD_or_SUB = C_in

  // Notes on the sheet:
  //   For Addition set C_in = 0
  //   For Subtraction set C_in = 1
endmodule

module _32_Bits_Ripple_Carry_Adder (
  input  [31:0] A,
  input  [31:0] B,
  input  C_in,
  output [31:0] SUM,
  output MSB
);

  wire C0, C1, C2, C3, multiplexer_1_out;
  wire [7:0] B0, B1, B2, B3;
  wire [31:0] not_1_out;

  Multiplexer #(.enable("false")) multiplexer_1 (.in0(1'b0), .in1(1'b1), .out(multiplexer_1_out), .sel(C_in));
  _8_Bits_Ripple_Carry_Adder u_8_bits_ripple_carry_adder_1 (
    .A(A[7:0]), .B(B0), .C_in(multiplexer_1_out), .A_B(SUM[7:0]), .C_out(C0));
  Multiplexer #(.width(32), .enable("false")) multiplexer_2 (
    .in0(B), .in1(not_1_out), .out({B3, B2, B1, B0}), .sel(C_in));
  assign not_1_out = ~B;  // NOT_Gate not_1, 32 bits wide
  _8_Bits_Ripple_Carry_Adder u_8_bits_ripple_carry_adder_2 (
    .A(A[15:8]), .B(B1), .C_in(C0), .A_B(SUM[15:8]), .C_out(C1));
  _8_Bits_Ripple_Carry_Adder u_8_bits_ripple_carry_adder_3 (
    .A(A[23:16]), .B(B2), .C_in(C1), .A_B(SUM[23:16]), .C_out(C2));
  _8_Bits_Ripple_Carry_Adder u_8_bits_ripple_carry_adder_4 (
    .A(A[31:24]), .B(B3), .C_in(C2), .A_B({MSB, SUM[30:24]}), .C_out(C3));

  assign SUM[31] = MSB;

  // Other names for the same wires on the sheet: A0[7:0] = A[7:0]; A1[7:0] = A[15:8]; A2[7:0] = A[23:16];
  //   A3[7:0] = A[31:24]; ADD_or_SUB = C_in; S0[7:0] = SUM[7:0]; S1[7:0] = SUM[15:8]; S2[7:0] = SUM[23:16];
  //   S3[7:0] = {MSB, SUM[30:24]}
endmodule

module Shift_Right (
  input  [15:0] A,
  input  [3:0] Select,
  output [15:0] A_Shifted
);

  // Probe on A
  Multiplexer #(.select(4), .width(15), .enable("false")) multiplexer_1 (
    .in0(A[14:0]), .in1(A[15:1]), .in2({{2{A[15]}}, A[14:2]}), .in3({{3{A[15]}}, A[14:3]}),
    .in4({{4{A[15]}}, A[14:4]}), .in5({{5{A[15]}}, A[14:5]}), .in6({{6{A[15]}}, A[14:6]}),
    .in7({{7{A[15]}}, A[14:7]}), .in8({{8{A[15]}}, A[14:8]}), .in9({{9{A[15]}}, A[14:9]}),
    .in10({{10{A[15]}}, A[14:10]}), .in11({{11{A[15]}}, A[14:11]}), .in12({{12{A[15]}}, A[14:12]}),
    .in13({{13{A[15]}}, A[14:13]}), .in14({{14{A[15]}}, A[14]}), .in15({15{A[15]}}), .out(A_Shifted[14:0]),
    .sel(Select));
  // Probe on {A[15], A_Shifted[14:0]}

  assign A_Shifted[15] = A[15];

  // Other names for the same wires on the sheet: d[15:0] = A; MSB = A[15]; Shift_1[14:0] = A[15:1];
  //   Shift_2[14:0] = {{2{A[15]}}, A[14:2]}; Shift_3[14:0] = {{3{A[15]}}, A[14:3]};
  //   Shift_4[14:0] = {{4{A[15]}}, A[14:4]}; Shift_5[14:0] = {{5{A[15]}}, A[14:5]};
  //   Shift_6[14:0] = {{6{A[15]}}, A[14:6]}; Shift_7[14:0] = {{7{A[15]}}, A[14:7]};
  //   Shift_8[14:0] = {{8{A[15]}}, A[14:8]}; Shift_9[14:0] = {{9{A[15]}}, A[14:9]};
  //   Shift_10[14:0] = {{10{A[15]}}, A[14:10]}; Shift_11[14:0] = {{11{A[15]}}, A[14:11]};
  //   Shift_12[14:0] = {{12{A[15]}}, A[14:12]}; Shift_13[14:0] = {{13{A[15]}}, A[14:13]};
  //   Shift_14[14:0] = {{14{A[15]}}, A[14]}; Shift_15[14:0] = {15{A[15]}}; AT[14:0] = A[14:0]
endmodule
