// Logisim project DIT_FFT_16_Point_16_Bits.circ as structural Verilog: 9 circuits, main circuit main
module main (
);

  wire [15:0] stage_four_1_y0_imag, stage_four_1_y0_real, stage_four_1_y1_imag, stage_four_1_y1_real,
       stage_four_1_y2_imag, stage_four_1_y2_real, stage_four_1_y3_imag, stage_four_1_y3_real,
       stage_four_1_y4_imag, stage_four_1_y4_real, stage_four_1_y5_imag, stage_four_1_y5_real,
       stage_four_1_y6_imag, stage_four_1_y6_real, stage_four_1_y7_imag, stage_four_1_y7_real,
       stage_four_1_y8_imag, stage_four_1_y8_real, stage_four_1_y9_imag, stage_four_1_y9_real,
       stage_four_1_y10_imag, stage_four_1_y10_real, stage_four_1_y11_imag, stage_four_1_y11_real,
       stage_four_1_y12_imag, stage_four_1_y12_real, stage_four_1_y13_imag, stage_four_1_y13_real,
       stage_four_1_y14_imag, stage_four_1_y14_real, stage_four_1_y15_real, stage_four_2_y0_imag,
       stage_four_2_y0_real, stage_four_2_y1_imag, stage_four_2_y1_real, stage_four_2_y2_imag,
       stage_four_2_y2_real, stage_four_2_y3_imag, stage_four_2_y3_real, stage_four_2_y4_imag,
       stage_four_2_y4_real, stage_four_2_y5_imag, stage_four_2_y5_real, stage_four_2_y6_imag,
       stage_four_2_y6_real, stage_four_2_y7_imag, stage_four_2_y7_real, stage_four_2_y8_imag,
       stage_four_2_y8_real, stage_four_2_y9_imag, stage_four_2_y9_real, stage_four_2_y10_imag,
       stage_four_2_y10_real, stage_four_2_y11_imag, stage_four_2_y11_real, stage_four_2_y12_imag,
       stage_four_2_y12_real, stage_four_2_y13_imag, stage_four_2_y13_real, stage_four_2_y14_imag,
       stage_four_2_y14_real, stage_four_2_y15_imag, stage_four_2_y15_real, stage_four_3_y0_imag,
       stage_four_3_y0_real, stage_four_3_y1_imag, stage_four_3_y1_real, stage_four_3_y2_imag,
       stage_four_3_y2_real, stage_four_3_y3_imag, stage_four_3_y3_real, stage_four_3_y4_imag,
       stage_four_3_y4_real, stage_four_3_y5_imag, stage_four_3_y5_real, stage_four_3_y6_imag,
       stage_four_3_y6_real, stage_four_3_y7_imag, stage_four_3_y7_real, stage_four_3_y8_imag,
       stage_four_3_y8_real, stage_four_3_y9_imag, stage_four_3_y9_real, stage_four_3_y10_imag,
       stage_four_3_y10_real, stage_four_3_y11_imag, stage_four_3_y11_real, stage_four_3_y12_imag,
       stage_four_3_y12_real, stage_four_3_y13_imag, stage_four_3_y13_real, stage_four_3_y14_imag,
       stage_four_3_y14_real, stage_four_3_y15_real, stage_one_1_y0_imag, stage_one_1_y0_real,
       stage_one_1_y1_imag, stage_one_1_y1_real, stage_one_1_y2_imag, stage_one_1_y2_real,
       stage_one_1_y3_imag, stage_one_1_y3_real, stage_one_1_y4_imag, stage_one_1_y4_real,
       stage_one_1_y5_imag, stage_one_1_y5_real, stage_one_1_y6_imag, stage_one_1_y6_real,
       stage_one_1_y7_imag, stage_one_1_y7_real, stage_one_1_y8_imag, stage_one_1_y8_real,
       stage_one_1_y9_imag, stage_one_1_y9_real, stage_one_1_y10_imag, stage_one_1_y10_real,
       stage_one_1_y11_imag, stage_one_1_y11_real, stage_one_1_y12_imag, stage_one_1_y12_real,
       stage_one_1_y13_imag, stage_one_1_y13_real, stage_one_1_y14_imag, stage_one_1_y14_real,
       stage_one_1_y15_imag, stage_one_1_y15_real, stage_one_2_y0_imag, stage_one_2_y0_real,
       stage_one_2_y1_imag, stage_one_2_y1_real, stage_one_2_y2_imag, stage_one_2_y2_real,
       stage_one_2_y3_imag, stage_one_2_y3_real, stage_one_2_y4_imag, stage_one_2_y4_real,
       stage_one_2_y5_imag, stage_one_2_y5_real, stage_one_2_y6_imag, stage_one_2_y6_real,
       stage_one_2_y7_imag, stage_one_2_y7_real, stage_one_2_y8_imag, stage_one_2_y8_real,
       stage_one_2_y9_imag, stage_one_2_y9_real, stage_one_2_y10_imag, stage_one_2_y10_real,
       stage_one_2_y11_imag, stage_one_2_y11_real, stage_one_2_y12_imag, stage_one_2_y12_real,
       stage_one_2_y13_imag, stage_one_2_y13_real, stage_one_2_y14_imag, stage_one_2_y14_real,
       stage_one_2_y15_imag, stage_one_2_y15_real, stage_one_3_y0_imag, stage_one_3_y0_real,
       stage_one_3_y1_imag, stage_one_3_y1_real, stage_one_3_y2_imag, stage_one_3_y2_real,
       stage_one_3_y3_imag, stage_one_3_y3_real, stage_one_3_y4_imag, stage_one_3_y4_real,
       stage_one_3_y5_imag, stage_one_3_y5_real, stage_one_3_y6_imag, stage_one_3_y6_real,
       stage_one_3_y7_imag, stage_one_3_y7_real, stage_one_3_y8_imag, stage_one_3_y8_real,
       stage_one_3_y9_imag, stage_one_3_y9_real, stage_one_3_y10_imag, stage_one_3_y10_real,
       stage_one_3_y11_imag, stage_one_3_y11_real, stage_one_3_y12_imag, stage_one_3_y12_real,
       stage_one_3_y13_imag, stage_one_3_y13_real, stage_one_3_y14_imag, stage_one_3_y14_real,
       stage_one_3_y15_imag, stage_one_3_y15_real, stage_three_1_y0_imag, stage_three_1_y0_real,
       stage_three_1_y1_imag, stage_three_1_y1_real, stage_three_1_y2_imag, stage_three_1_y2_real,
       stage_three_1_y3_imag, stage_three_1_y3_real, stage_three_1_y4_imag, stage_three_1_y4_real,
       stage_three_1_y5_imag, stage_three_1_y5_real, stage_three_1_y6_imag, stage_three_1_y6_real,
       stage_three_1_y7_imag, stage_three_1_y7_real, stage_three_1_y8_imag, stage_three_1_y8_real,
       stage_three_1_y9_imag, stage_three_1_y9_real, stage_three_1_y10_imag, stage_three_1_y10_real,
       stage_three_1_y11_imag, stage_three_1_y11_real, stage_three_1_y12_imag, stage_three_1_y12_real,
       stage_three_1_y13_imag, stage_three_1_y13_real, stage_three_1_y14_imag, stage_three_1_y14_real,
       stage_three_1_y15_imag, stage_three_1_y15_real, stage_three_2_y0_imag, stage_three_2_y0_real,
       stage_three_2_y1_imag, stage_three_2_y1_real, stage_three_2_y2_imag, stage_three_2_y2_real,
       stage_three_2_y3_imag, stage_three_2_y3_real, stage_three_2_y4_imag, stage_three_2_y4_real,
       stage_three_2_y5_imag, stage_three_2_y5_real, stage_three_2_y6_imag, stage_three_2_y6_real,
       stage_three_2_y7_imag, stage_three_2_y7_real, stage_three_2_y8_imag, stage_three_2_y8_real,
       stage_three_2_y9_imag, stage_three_2_y9_real, stage_three_2_y10_imag, stage_three_2_y10_real,
       stage_three_2_y11_imag, stage_three_2_y11_real, stage_three_2_y12_imag, stage_three_2_y12_real,
       stage_three_2_y13_imag, stage_three_2_y13_real, stage_three_2_y14_imag, stage_three_2_y14_real,
       stage_three_2_y15_imag, stage_three_2_y15_real, stage_three_3_y0_imag, stage_three_3_y0_real,
       stage_three_3_y1_imag, stage_three_3_y1_real, stage_three_3_y2_imag, stage_three_3_y2_real,
       stage_three_3_y3_imag, stage_three_3_y3_real, stage_three_3_y4_imag, stage_three_3_y4_real,
       stage_three_3_y5_imag, stage_three_3_y5_real, stage_three_3_y6_imag, stage_three_3_y6_real,
       stage_three_3_y7_imag, stage_three_3_y7_real, stage_three_3_y8_imag, stage_three_3_y8_real,
       stage_three_3_y9_imag, stage_three_3_y9_real, stage_three_3_y10_imag, stage_three_3_y10_real,
       stage_three_3_y11_imag, stage_three_3_y11_real, stage_three_3_y12_imag, stage_three_3_y12_real,
       stage_three_3_y13_imag, stage_three_3_y13_real, stage_three_3_y14_imag, stage_three_3_y14_real,
       stage_three_3_y15_imag, stage_three_3_y15_real, stage_two_1_y0_imag, stage_two_1_y0_real,
       stage_two_1_y1_imag, stage_two_1_y1_real, stage_two_1_y2_imag, stage_two_1_y2_real,
       stage_two_1_y3_imag, stage_two_1_y3_real, stage_two_1_y4_imag, stage_two_1_y4_real,
       stage_two_1_y5_imag, stage_two_1_y5_real, stage_two_1_y6_imag, stage_two_1_y6_real,
       stage_two_1_y7_imag, stage_two_1_y7_real, stage_two_1_y8_imag, stage_two_1_y8_real,
       stage_two_1_y9_imag, stage_two_1_y9_real, stage_two_1_y10_imag, stage_two_1_y10_real,
       stage_two_1_y11_imag, stage_two_1_y11_real, stage_two_1_y12_imag, stage_two_1_y12_real,
       stage_two_1_y13_imag, stage_two_1_y13_real, stage_two_1_y14_imag, stage_two_1_y14_real,
       stage_two_1_y15_imag, stage_two_1_y15_real, stage_two_2_y0_imag, stage_two_2_y0_real,
       stage_two_2_y1_imag, stage_two_2_y1_real, stage_two_2_y2_imag, stage_two_2_y2_real,
       stage_two_2_y3_imag, stage_two_2_y3_real, stage_two_2_y4_imag, stage_two_2_y4_real,
       stage_two_2_y5_imag, stage_two_2_y5_real, stage_two_2_y6_imag, stage_two_2_y6_real,
       stage_two_2_y7_imag, stage_two_2_y7_real, stage_two_2_y8_imag, stage_two_2_y8_real,
       stage_two_2_y9_imag, stage_two_2_y9_real, stage_two_2_y10_imag, stage_two_2_y10_real,
       stage_two_2_y11_imag, stage_two_2_y11_real, stage_two_2_y12_imag, stage_two_2_y12_real,
       stage_two_2_y13_imag, stage_two_2_y13_real, stage_two_2_y14_imag, stage_two_2_y14_real,
       stage_two_2_y15_imag, stage_two_2_y15_real, stage_two_3_y0_imag, stage_two_3_y0_real,
       stage_two_3_y1_imag, stage_two_3_y1_real, stage_two_3_y2_imag, stage_two_3_y2_real,
       stage_two_3_y3_imag, stage_two_3_y3_real, stage_two_3_y4_imag, stage_two_3_y4_real,
       stage_two_3_y5_imag, stage_two_3_y5_real, stage_two_3_y6_imag, stage_two_3_y6_real,
       stage_two_3_y7_imag, stage_two_3_y7_real, stage_two_3_y8_imag, stage_two_3_y8_real,
       stage_two_3_y9_imag, stage_two_3_y9_real, stage_two_3_y10_imag, stage_two_3_y10_real,
       stage_two_3_y11_imag, stage_two_3_y11_real, stage_two_3_y12_imag, stage_two_3_y12_real,
       stage_two_3_y13_imag, stage_two_3_y13_real, stage_two_3_y14_imag, stage_two_3_y14_real,
       stage_two_3_y15_imag, stage_two_3_y15_real;

  Stage_One stage_one_1 (
    .x0_real(16'h1), .x0_imag({16{1'b0}}), .x1_real(16'h1), .x1_imag({16{1'b0}}), .x2_real(16'h1),
    .x2_imag({16{1'b0}}), .x3_real(16'h1), .x3_imag({16{1'b0}}), .x4_real(16'h1), .x4_imag({16{1'b0}}),
    .x5_real(16'h1), .x5_imag({16{1'b0}}), .x6_real(16'h1), .x6_imag({16{1'b0}}), .x7_real(16'h1),
    .x7_imag({16{1'b0}}), .x8_real(16'h1), .x8_imag({16{1'b0}}), .x9_real(16'h1), .x9_imag({16{1'b0}}),
    .x10_real(16'h1), .x10_imag({16{1'b0}}), .x11_real(16'h1), .x11_imag({16{1'b0}}), .x12_real(16'h1),
    .x12_imag({16{1'b0}}), .x13_real(16'h1), .x13_imag({16{1'b0}}), .x14_real(16'h1), .x14_imag({16{1'b0}}),
    .x15_real(16'h1), .x15_imag({16{1'b0}}), .y0_real(stage_one_1_y0_real), .y0_imag(stage_one_1_y0_imag),
    .y1_real(stage_one_1_y1_real), .y1_imag(stage_one_1_y1_imag), .y2_real(stage_one_1_y2_real),
    .y2_imag(stage_one_1_y2_imag), .y3_real(stage_one_1_y3_real), .y3_imag(stage_one_1_y3_imag),
    .y4_real(stage_one_1_y4_real), .y4_imag(stage_one_1_y4_imag), .y5_real(stage_one_1_y5_real),
    .y5_imag(stage_one_1_y5_imag), .y6_real(stage_one_1_y6_real), .y6_imag(stage_one_1_y6_imag),
    .y7_real(stage_one_1_y7_real), .y7_imag(stage_one_1_y7_imag), .y8_real(stage_one_1_y8_real),
    .y8_imag(stage_one_1_y8_imag), .y9_real(stage_one_1_y9_real), .y9_imag(stage_one_1_y9_imag),
    .y10_real(stage_one_1_y10_real), .y10_imag(stage_one_1_y10_imag), .y11_real(stage_one_1_y11_real),
    .y11_imag(stage_one_1_y11_imag), .y12_real(stage_one_1_y12_real), .y12_imag(stage_one_1_y12_imag),
    .y13_real(stage_one_1_y13_real), .y13_imag(stage_one_1_y13_imag), .y14_real(stage_one_1_y14_real),
    .y14_imag(stage_one_1_y14_imag), .y15_real(stage_one_1_y15_real), .y15_imag(stage_one_1_y15_imag));
  Stage_One stage_one_2 (
    .x0_real(16'h20), .x0_imag({16{1'b0}}), .x1_real({16{1'b0}}), .x1_imag({16{1'b0}}), .x2_real({16{1'b0}}),
    .x2_imag({16{1'b0}}), .x3_real({16{1'b0}}), .x3_imag({16{1'b0}}), .x4_real({16{1'b0}}),
    .x4_imag({16{1'b0}}), .x5_real({16{1'b0}}), .x5_imag({16{1'b0}}), .x6_real({16{1'b0}}),
    .x6_imag({16{1'b0}}), .x7_real({16{1'b0}}), .x7_imag({16{1'b0}}), .x8_real({16{1'b0}}),
    .x8_imag({16{1'b0}}), .x9_real({16{1'b0}}), .x9_imag({16{1'b0}}), .x10_real({16{1'b0}}),
    .x10_imag({16{1'b0}}), .x11_real({16{1'b0}}), .x11_imag({16{1'b0}}), .x12_real({16{1'b0}}),
    .x12_imag({16{1'b0}}), .x13_real({16{1'b0}}), .x13_imag({16{1'b0}}), .x14_real({16{1'b0}}),
    .x14_imag({16{1'b0}}), .x15_real({16{1'b0}}), .x15_imag({16{1'b0}}), .y0_real(stage_one_2_y0_real),
    .y0_imag(stage_one_2_y0_imag), .y1_real(stage_one_2_y1_real), .y1_imag(stage_one_2_y1_imag),
    .y2_real(stage_one_2_y2_real), .y2_imag(stage_one_2_y2_imag), .y3_real(stage_one_2_y3_real),
    .y3_imag(stage_one_2_y3_imag), .y4_real(stage_one_2_y4_real), .y4_imag(stage_one_2_y4_imag),
    .y5_real(stage_one_2_y5_real), .y5_imag(stage_one_2_y5_imag), .y6_real(stage_one_2_y6_real),
    .y6_imag(stage_one_2_y6_imag), .y7_real(stage_one_2_y7_real), .y7_imag(stage_one_2_y7_imag),
    .y8_real(stage_one_2_y8_real), .y8_imag(stage_one_2_y8_imag), .y9_real(stage_one_2_y9_real),
    .y9_imag(stage_one_2_y9_imag), .y10_real(stage_one_2_y10_real), .y10_imag(stage_one_2_y10_imag),
    .y11_real(stage_one_2_y11_real), .y11_imag(stage_one_2_y11_imag), .y12_real(stage_one_2_y12_real),
    .y12_imag(stage_one_2_y12_imag), .y13_real(stage_one_2_y13_real), .y13_imag(stage_one_2_y13_imag),
    .y14_real(stage_one_2_y14_real), .y14_imag(stage_one_2_y14_imag), .y15_real(stage_one_2_y15_real),
    .y15_imag(stage_one_2_y15_imag));
  Stage_Two stage_two_1 (
    .x0_real(stage_one_1_y0_real), .x0_imag(stage_one_1_y0_imag), .x1_real(stage_one_1_y1_real),
    .x1_imag(stage_one_1_y1_imag), .x2_real(stage_one_1_y2_real), .x2_imag(stage_one_1_y2_imag),
    .x3_real(stage_one_1_y3_real), .x3_imag(stage_one_1_y3_imag), .x4_real(stage_one_1_y4_real),
    .x4_imag(stage_one_1_y4_imag), .x5_real(stage_one_1_y5_real), .x5_imag(stage_one_1_y5_imag),
    .x6_real(stage_one_1_y6_real), .x6_imag(stage_one_1_y6_imag), .x7_real(stage_one_1_y7_real),
    .x7_imag(stage_one_1_y7_imag), .x8_real(stage_one_1_y8_real), .x8_imag(stage_one_1_y8_imag),
    .x9_real(stage_one_1_y9_real), .x9_imag(stage_one_1_y9_imag), .x10_real(stage_one_1_y10_real),
    .x10_imag(stage_one_1_y10_imag), .x11_real(stage_one_1_y11_real), .x11_imag(stage_one_1_y11_imag),
    .x12_real(stage_one_1_y12_real), .x12_imag(stage_one_1_y12_imag), .x13_real(stage_one_1_y13_real),
    .x13_imag(stage_one_1_y13_imag), .x14_real(stage_one_1_y14_real), .x14_imag(stage_one_1_y14_imag),
    .x15_real(stage_one_1_y15_real), .x15_imag(stage_one_1_y15_imag), .y0_real(stage_two_1_y0_real),
    .y0_imag(stage_two_1_y0_imag), .y1_real(stage_two_1_y1_real), .y1_imag(stage_two_1_y1_imag),
    .y2_real(stage_two_1_y2_real), .y2_imag(stage_two_1_y2_imag), .y3_real(stage_two_1_y3_real),
    .y3_imag(stage_two_1_y3_imag), .y4_real(stage_two_1_y4_real), .y4_imag(stage_two_1_y4_imag),
    .y5_real(stage_two_1_y5_real), .y5_imag(stage_two_1_y5_imag), .y6_real(stage_two_1_y6_real),
    .y6_imag(stage_two_1_y6_imag), .y7_real(stage_two_1_y7_real), .y7_imag(stage_two_1_y7_imag),
    .y8_real(stage_two_1_y8_real), .y8_imag(stage_two_1_y8_imag), .y9_real(stage_two_1_y9_real),
    .y9_imag(stage_two_1_y9_imag), .y10_real(stage_two_1_y10_real), .y10_imag(stage_two_1_y10_imag),
    .y11_real(stage_two_1_y11_real), .y11_imag(stage_two_1_y11_imag), .y12_real(stage_two_1_y12_real),
    .y12_imag(stage_two_1_y12_imag), .y13_real(stage_two_1_y13_real), .y13_imag(stage_two_1_y13_imag),
    .y14_real(stage_two_1_y14_real), .y14_imag(stage_two_1_y14_imag), .y15_real(stage_two_1_y15_real),
    .y15_imag(stage_two_1_y15_imag));
  Stage_Two stage_two_2 (
    .x0_real(stage_one_2_y0_real), .x0_imag(stage_one_2_y0_imag), .x1_real(stage_one_2_y1_real),
    .x1_imag(stage_one_2_y1_imag), .x2_real(stage_one_2_y2_real), .x2_imag(stage_one_2_y2_imag),
    .x3_real(stage_one_2_y3_real), .x3_imag(stage_one_2_y3_imag), .x4_real(stage_one_2_y4_real),
    .x4_imag(stage_one_2_y4_imag), .x5_real(stage_one_2_y5_real), .x5_imag(stage_one_2_y5_imag),
    .x6_real(stage_one_2_y6_real), .x6_imag(stage_one_2_y6_imag), .x7_real(stage_one_2_y7_real),
    .x7_imag(stage_one_2_y7_imag), .x8_real(stage_one_2_y8_real), .x8_imag(stage_one_2_y8_imag),
    .x9_real(stage_one_2_y9_real), .x9_imag(stage_one_2_y9_imag), .x10_real(stage_one_2_y10_real),
    .x10_imag(stage_one_2_y10_imag), .x11_real(stage_one_2_y11_real), .x11_imag(stage_one_2_y11_imag),
    .x12_real(stage_one_2_y12_real), .x12_imag(stage_one_2_y12_imag), .x13_real(stage_one_2_y13_real),
    .x13_imag(stage_one_2_y13_imag), .x14_real(stage_one_2_y14_real), .x14_imag(stage_one_2_y14_imag),
    .x15_real(stage_one_2_y15_real), .x15_imag(stage_one_2_y15_imag), .y0_real(stage_two_2_y0_real),
    .y0_imag(stage_two_2_y0_imag), .y1_real(stage_two_2_y1_real), .y1_imag(stage_two_2_y1_imag),
    .y2_real(stage_two_2_y2_real), .y2_imag(stage_two_2_y2_imag), .y3_real(stage_two_2_y3_real),
    .y3_imag(stage_two_2_y3_imag), .y4_real(stage_two_2_y4_real), .y4_imag(stage_two_2_y4_imag),
    .y5_real(stage_two_2_y5_real), .y5_imag(stage_two_2_y5_imag), .y6_real(stage_two_2_y6_real),
    .y6_imag(stage_two_2_y6_imag), .y7_real(stage_two_2_y7_real), .y7_imag(stage_two_2_y7_imag),
    .y8_real(stage_two_2_y8_real), .y8_imag(stage_two_2_y8_imag), .y9_real(stage_two_2_y9_real),
    .y9_imag(stage_two_2_y9_imag), .y10_real(stage_two_2_y10_real), .y10_imag(stage_two_2_y10_imag),
    .y11_real(stage_two_2_y11_real), .y11_imag(stage_two_2_y11_imag), .y12_real(stage_two_2_y12_real),
    .y12_imag(stage_two_2_y12_imag), .y13_real(stage_two_2_y13_real), .y13_imag(stage_two_2_y13_imag),
    .y14_real(stage_two_2_y14_real), .y14_imag(stage_two_2_y14_imag), .y15_real(stage_two_2_y15_real),
    .y15_imag(stage_two_2_y15_imag));
  Stage_Three stage_three_1 (
    .x0_real(stage_two_1_y0_real), .x0_imag(stage_two_1_y0_imag), .x1_real(stage_two_1_y1_real),
    .x1_imag(stage_two_1_y1_imag), .x2_real(stage_two_1_y2_real), .x2_imag(stage_two_1_y2_imag),
    .x3_real(stage_two_1_y3_real), .x3_imag(stage_two_1_y3_imag), .x4_real(stage_two_1_y4_real),
    .x4_imag(stage_two_1_y4_imag), .x5_real(stage_two_1_y5_real), .x5_imag(stage_two_1_y5_imag),
    .x6_real(stage_two_1_y6_real), .x6_imag(stage_two_1_y6_imag), .x7_real(stage_two_1_y7_real),
    .x7_imag(stage_two_1_y7_imag), .x8_real(stage_two_1_y8_real), .x8_imag(stage_two_1_y8_imag),
    .x9_real(stage_two_1_y9_real), .x9_imag(stage_two_1_y9_imag), .x10_real(stage_two_1_y10_real),
    .x10_imag(stage_two_1_y10_imag), .x11_real(stage_two_1_y11_real), .x11_imag(stage_two_1_y11_imag),
    .x12_real(stage_two_1_y12_real), .x12_imag(stage_two_1_y12_imag), .x13_real(stage_two_1_y13_real),
    .x13_imag(stage_two_1_y13_imag), .x14_real(stage_two_1_y14_real), .x14_imag(stage_two_1_y14_imag),
    .x15_real(stage_two_1_y15_real), .x15_imag(stage_two_1_y15_imag), .y0_real(stage_three_1_y0_real),
    .y0_imag(stage_three_1_y0_imag), .y1_real(stage_three_1_y1_real), .y1_imag(stage_three_1_y1_imag),
    .y2_real(stage_three_1_y2_real), .y2_imag(stage_three_1_y2_imag), .y3_real(stage_three_1_y3_real),
    .y3_imag(stage_three_1_y3_imag), .y4_real(stage_three_1_y4_real), .y4_imag(stage_three_1_y4_imag),
    .y5_real(stage_three_1_y5_real), .y5_imag(stage_three_1_y5_imag), .y6_real(stage_three_1_y6_real),
    .y6_imag(stage_three_1_y6_imag), .y7_real(stage_three_1_y7_real), .y7_imag(stage_three_1_y7_imag),
    .y8_real(stage_three_1_y8_real), .y8_imag(stage_three_1_y8_imag), .y9_real(stage_three_1_y9_real),
    .y9_imag(stage_three_1_y9_imag), .y10_real(stage_three_1_y10_real), .y10_imag(stage_three_1_y10_imag),
    .y11_real(stage_three_1_y11_real), .y11_imag(stage_three_1_y11_imag), .y12_real(stage_three_1_y12_real),
    .y12_imag(stage_three_1_y12_imag), .y13_real(stage_three_1_y13_real), .y13_imag(stage_three_1_y13_imag),
    .y14_real(stage_three_1_y14_real), .y14_imag(stage_three_1_y14_imag), .y15_real(stage_three_1_y15_real),
    .y15_imag(stage_three_1_y15_imag));
  Stage_Three stage_three_2 (
    .x0_real(stage_two_2_y0_real), .x0_imag(stage_two_2_y0_imag), .x1_real(stage_two_2_y1_real),
    .x1_imag(stage_two_2_y1_imag), .x2_real(stage_two_2_y2_real), .x2_imag(stage_two_2_y2_imag),
    .x3_real(stage_two_2_y3_real), .x3_imag(stage_two_2_y3_imag), .x4_real(stage_two_2_y4_real),
    .x4_imag(stage_two_2_y4_imag), .x5_real(stage_two_2_y5_real), .x5_imag(stage_two_2_y5_imag),
    .x6_real(stage_two_2_y6_real), .x6_imag(stage_two_2_y6_imag), .x7_real(stage_two_2_y7_real),
    .x7_imag(stage_two_2_y7_imag), .x8_real(stage_two_2_y8_real), .x8_imag(stage_two_2_y8_imag),
    .x9_real(stage_two_2_y9_real), .x9_imag(stage_two_2_y9_imag), .x10_real(stage_two_2_y10_real),
    .x10_imag(stage_two_2_y10_imag), .x11_real(stage_two_2_y11_real), .x11_imag(stage_two_2_y11_imag),
    .x12_real(stage_two_2_y12_real), .x12_imag(stage_two_2_y12_imag), .x13_real(stage_two_2_y13_real),
    .x13_imag(stage_two_2_y13_imag), .x14_real(stage_two_2_y14_real), .x14_imag(stage_two_2_y14_imag),
    .x15_real(stage_two_2_y15_real), .x15_imag(stage_two_2_y15_imag), .y0_real(stage_three_2_y0_real),
    .y0_imag(stage_three_2_y0_imag), .y1_real(stage_three_2_y1_real), .y1_imag(stage_three_2_y1_imag),
    .y2_real(stage_three_2_y2_real), .y2_imag(stage_three_2_y2_imag), .y3_real(stage_three_2_y3_real),
    .y3_imag(stage_three_2_y3_imag), .y4_real(stage_three_2_y4_real), .y4_imag(stage_three_2_y4_imag),
    .y5_real(stage_three_2_y5_real), .y5_imag(stage_three_2_y5_imag), .y6_real(stage_three_2_y6_real),
    .y6_imag(stage_three_2_y6_imag), .y7_real(stage_three_2_y7_real), .y7_imag(stage_three_2_y7_imag),
    .y8_real(stage_three_2_y8_real), .y8_imag(stage_three_2_y8_imag), .y9_real(stage_three_2_y9_real),
    .y9_imag(stage_three_2_y9_imag), .y10_real(stage_three_2_y10_real), .y10_imag(stage_three_2_y10_imag),
    .y11_real(stage_three_2_y11_real), .y11_imag(stage_three_2_y11_imag), .y12_real(stage_three_2_y12_real),
    .y12_imag(stage_three_2_y12_imag), .y13_real(stage_three_2_y13_real), .y13_imag(stage_three_2_y13_imag),
    .y14_real(stage_three_2_y14_real), .y14_imag(stage_three_2_y14_imag), .y15_real(stage_three_2_y15_real),
    .y15_imag(stage_three_2_y15_imag));
  // Probe on stage_four_1_y0_real
  Stage_Four stage_four_1 (
    .x0_real(stage_three_1_y0_real), .x0_imag(stage_three_1_y0_imag), .x1_real(stage_three_1_y1_real),
    .x1_imag(stage_three_1_y1_imag), .x2_real(stage_three_1_y2_real), .x2_imag(stage_three_1_y2_imag),
    .x3_real(stage_three_1_y3_real), .x3_imag(stage_three_1_y3_imag), .x4_real(stage_three_1_y4_real),
    .x4_imag(stage_three_1_y4_imag), .x5_real(stage_three_1_y5_real), .x5_imag(stage_three_1_y5_imag),
    .x6_real(stage_three_1_y6_real), .x6_imag(stage_three_1_y6_imag), .x7_real(stage_three_1_y7_real),
    .x7_imag(stage_three_1_y7_imag), .x8_real(stage_three_1_y8_real), .x8_imag(stage_three_1_y8_imag),
    .x9_real(stage_three_1_y9_real), .x9_imag(stage_three_1_y9_imag), .x10_real(stage_three_1_y10_real),
    .x10_imag(stage_three_1_y10_imag), .x11_real(stage_three_1_y11_real), .x11_imag(stage_three_1_y11_imag),
    .x12_real(stage_three_1_y12_real), .x12_imag(stage_three_1_y12_imag), .x13_real(stage_three_1_y13_real),
    .x13_imag(stage_three_1_y13_imag), .x14_real(stage_three_1_y14_real), .x14_imag(stage_three_1_y14_imag),
    .x15_real(stage_three_1_y15_real), .x15_imag(stage_three_1_y15_imag), .y0_real(stage_four_1_y0_real),
    .y0_imag(stage_four_1_y0_imag), .y1_real(stage_four_1_y1_real), .y1_imag(stage_four_1_y1_imag),
    .y2_real(stage_four_1_y2_real), .y2_imag(stage_four_1_y2_imag), .y3_real(stage_four_1_y3_real),
    .y3_imag(stage_four_1_y3_imag), .y4_real(stage_four_1_y4_real), .y4_imag(stage_four_1_y4_imag),
    .y5_real(stage_four_1_y5_real), .y5_imag(stage_four_1_y5_imag), .y6_real(stage_four_1_y6_real),
    .y6_imag(stage_four_1_y6_imag), .y7_real(stage_four_1_y7_real), .y7_imag(stage_four_1_y7_imag),
    .y8_real(stage_four_1_y8_real), .y8_imag(stage_four_1_y8_imag), .y9_real(stage_four_1_y9_real),
    .y9_imag(stage_four_1_y9_imag), .y10_real(stage_four_1_y10_real), .y10_imag(stage_four_1_y10_imag),
    .y11_real(stage_four_1_y11_real), .y11_imag(stage_four_1_y11_imag), .y12_real(stage_four_1_y12_real),
    .y12_imag(stage_four_1_y12_imag), .y13_real(stage_four_1_y13_real), .y13_imag(stage_four_1_y13_imag),
    .y14_real(stage_four_1_y14_real), .y14_imag(stage_four_1_y14_imag), .y15_real(stage_four_1_y15_real));  // open: y15_imag
  // Probe on stage_four_1_y1_real
  // Probe on stage_four_1_y2_real
  // Probe on stage_four_1_y3_real
  // Probe on stage_four_1_y4_real
  // Probe on stage_four_1_y5_real
  // Probe on stage_four_1_y6_real
  // Probe on stage_four_1_y7_real
  // Probe on stage_four_1_y8_real
  // Probe on stage_four_1_y9_real
  // Probe on stage_four_1_y10_real
  // Probe on stage_four_1_y11_real
  // Probe on stage_four_1_y12_real
  // Probe on stage_four_1_y13_real
  // Probe on stage_four_1_y14_real
  // Probe on stage_four_1_y15_real
  Stage_Four stage_four_2 (
    .x0_real(stage_three_2_y0_real), .x0_imag(stage_three_2_y0_imag), .x1_real(stage_three_2_y1_real),
    .x1_imag(stage_three_2_y1_imag), .x2_real(stage_three_2_y2_real), .x2_imag(stage_three_2_y2_imag),
    .x3_real(stage_three_2_y3_real), .x3_imag(stage_three_2_y3_imag), .x4_real(stage_three_2_y4_real),
    .x4_imag(stage_three_2_y4_imag), .x5_real(stage_three_2_y5_real), .x5_imag(stage_three_2_y5_imag),
    .x6_real(stage_three_2_y6_real), .x6_imag(stage_three_2_y6_imag), .x7_real(stage_three_2_y7_real),
    .x7_imag(stage_three_2_y7_imag), .x8_real(stage_three_2_y8_real), .x8_imag(stage_three_2_y8_imag),
    .x9_real(stage_three_2_y9_real), .x9_imag(stage_three_2_y9_imag), .x10_real(stage_three_2_y10_real),
    .x10_imag(stage_three_2_y10_imag), .x11_real(stage_three_2_y11_real), .x11_imag(stage_three_2_y11_imag),
    .x12_real(stage_three_2_y12_real), .x12_imag(stage_three_2_y12_imag), .x13_real(stage_three_2_y13_real),
    .x13_imag(stage_three_2_y13_imag), .x14_real(stage_three_2_y14_real), .x14_imag(stage_three_2_y14_imag),
    .x15_real(stage_three_2_y15_real), .x15_imag(stage_three_2_y15_imag), .y0_real(stage_four_2_y0_real),
    .y0_imag(stage_four_2_y0_imag), .y1_real(stage_four_2_y1_real), .y1_imag(stage_four_2_y1_imag),
    .y2_real(stage_four_2_y2_real), .y2_imag(stage_four_2_y2_imag), .y3_real(stage_four_2_y3_real),
    .y3_imag(stage_four_2_y3_imag), .y4_real(stage_four_2_y4_real), .y4_imag(stage_four_2_y4_imag),
    .y5_real(stage_four_2_y5_real), .y5_imag(stage_four_2_y5_imag), .y6_real(stage_four_2_y6_real),
    .y6_imag(stage_four_2_y6_imag), .y7_real(stage_four_2_y7_real), .y7_imag(stage_four_2_y7_imag),
    .y8_real(stage_four_2_y8_real), .y8_imag(stage_four_2_y8_imag), .y9_real(stage_four_2_y9_real),
    .y9_imag(stage_four_2_y9_imag), .y10_real(stage_four_2_y10_real), .y10_imag(stage_four_2_y10_imag),
    .y11_real(stage_four_2_y11_real), .y11_imag(stage_four_2_y11_imag), .y12_real(stage_four_2_y12_real),
    .y12_imag(stage_four_2_y12_imag), .y13_real(stage_four_2_y13_real), .y13_imag(stage_four_2_y13_imag),
    .y14_real(stage_four_2_y14_real), .y14_imag(stage_four_2_y14_imag), .y15_real(stage_four_2_y15_real),
    .y15_imag(stage_four_2_y15_imag));
  // Probe on stage_four_2_y0_real
  // Probe on stage_four_2_y1_real
  // Probe on stage_four_2_y2_real
  // Probe on stage_four_2_y3_real
  // Probe on stage_four_2_y4_real
  // Probe on stage_four_2_y5_real
  // Probe on stage_four_2_y6_real
  // Probe on stage_four_2_y7_real
  // Probe on stage_four_2_y8_real
  // Probe on stage_four_2_y9_real
  // Probe on stage_four_2_y10_real
  // Probe on stage_four_2_y11_real
  // Probe on stage_four_2_y12_real
  // Probe on stage_four_2_y13_real
  // Probe on stage_four_2_y14_real
  // Probe on stage_four_2_y15_real
  Stage_One stage_one_3 (
    .x0_real(16'h10), .x0_imag({16{1'b0}}), .x1_real({16{1'b0}}), .x1_imag({16{1'b0}}), .x2_real(16'hfff0),
    .x2_imag({16{1'b0}}), .x3_real({16{1'b0}}), .x3_imag({16{1'b0}}), .x4_real(16'h10), .x4_imag({16{1'b0}}),
    .x5_real({16{1'b0}}), .x5_imag({16{1'b0}}), .x6_real(16'hfff0), .x6_imag({16{1'b0}}),
    .x7_real({16{1'b0}}), .x7_imag({16{1'b0}}), .x8_real(16'h10), .x8_imag({16{1'b0}}), .x9_real({16{1'b0}}),
    .x9_imag({16{1'b0}}), .x10_real(16'hfff0), .x10_imag({16{1'b0}}), .x11_real({16{1'b0}}),
    .x11_imag({16{1'b0}}), .x12_real(16'h10), .x12_imag({16{1'b0}}), .x13_real({16{1'b0}}),
    .x13_imag({16{1'b0}}), .x14_real(16'hfff0), .x14_imag({16{1'b0}}), .x15_real({16{1'b0}}),
    .x15_imag({16{1'b0}}), .y0_real(stage_one_3_y0_real), .y0_imag(stage_one_3_y0_imag),
    .y1_real(stage_one_3_y1_real), .y1_imag(stage_one_3_y1_imag), .y2_real(stage_one_3_y2_real),
    .y2_imag(stage_one_3_y2_imag), .y3_real(stage_one_3_y3_real), .y3_imag(stage_one_3_y3_imag),
    .y4_real(stage_one_3_y4_real), .y4_imag(stage_one_3_y4_imag), .y5_real(stage_one_3_y5_real),
    .y5_imag(stage_one_3_y5_imag), .y6_real(stage_one_3_y6_real), .y6_imag(stage_one_3_y6_imag),
    .y7_real(stage_one_3_y7_real), .y7_imag(stage_one_3_y7_imag), .y8_real(stage_one_3_y8_real),
    .y8_imag(stage_one_3_y8_imag), .y9_real(stage_one_3_y9_real), .y9_imag(stage_one_3_y9_imag),
    .y10_real(stage_one_3_y10_real), .y10_imag(stage_one_3_y10_imag), .y11_real(stage_one_3_y11_real),
    .y11_imag(stage_one_3_y11_imag), .y12_real(stage_one_3_y12_real), .y12_imag(stage_one_3_y12_imag),
    .y13_real(stage_one_3_y13_real), .y13_imag(stage_one_3_y13_imag), .y14_real(stage_one_3_y14_real),
    .y14_imag(stage_one_3_y14_imag), .y15_real(stage_one_3_y15_real), .y15_imag(stage_one_3_y15_imag));
  Stage_Two stage_two_3 (
    .x0_real(stage_one_3_y0_real), .x0_imag(stage_one_3_y0_imag), .x1_real(stage_one_3_y1_real),
    .x1_imag(stage_one_3_y1_imag), .x2_real(stage_one_3_y2_real), .x2_imag(stage_one_3_y2_imag),
    .x3_real(stage_one_3_y3_real), .x3_imag(stage_one_3_y3_imag), .x4_real(stage_one_3_y4_real),
    .x4_imag(stage_one_3_y4_imag), .x5_real(stage_one_3_y5_real), .x5_imag(stage_one_3_y5_imag),
    .x6_real(stage_one_3_y6_real), .x6_imag(stage_one_3_y6_imag), .x7_real(stage_one_3_y7_real),
    .x7_imag(stage_one_3_y7_imag), .x8_real(stage_one_3_y8_real), .x8_imag(stage_one_3_y8_imag),
    .x9_real(stage_one_3_y9_real), .x9_imag(stage_one_3_y9_imag), .x10_real(stage_one_3_y10_real),
    .x10_imag(stage_one_3_y10_imag), .x11_real(stage_one_3_y11_real), .x11_imag(stage_one_3_y11_imag),
    .x12_real(stage_one_3_y12_real), .x12_imag(stage_one_3_y12_imag), .x13_real(stage_one_3_y13_real),
    .x13_imag(stage_one_3_y13_imag), .x14_real(stage_one_3_y14_real), .x14_imag(stage_one_3_y14_imag),
    .x15_real(stage_one_3_y15_real), .x15_imag(stage_one_3_y15_imag), .y0_real(stage_two_3_y0_real),
    .y0_imag(stage_two_3_y0_imag), .y1_real(stage_two_3_y1_real), .y1_imag(stage_two_3_y1_imag),
    .y2_real(stage_two_3_y2_real), .y2_imag(stage_two_3_y2_imag), .y3_real(stage_two_3_y3_real),
    .y3_imag(stage_two_3_y3_imag), .y4_real(stage_two_3_y4_real), .y4_imag(stage_two_3_y4_imag),
    .y5_real(stage_two_3_y5_real), .y5_imag(stage_two_3_y5_imag), .y6_real(stage_two_3_y6_real),
    .y6_imag(stage_two_3_y6_imag), .y7_real(stage_two_3_y7_real), .y7_imag(stage_two_3_y7_imag),
    .y8_real(stage_two_3_y8_real), .y8_imag(stage_two_3_y8_imag), .y9_real(stage_two_3_y9_real),
    .y9_imag(stage_two_3_y9_imag), .y10_real(stage_two_3_y10_real), .y10_imag(stage_two_3_y10_imag),
    .y11_real(stage_two_3_y11_real), .y11_imag(stage_two_3_y11_imag), .y12_real(stage_two_3_y12_real),
    .y12_imag(stage_two_3_y12_imag), .y13_real(stage_two_3_y13_real), .y13_imag(stage_two_3_y13_imag),
    .y14_real(stage_two_3_y14_real), .y14_imag(stage_two_3_y14_imag), .y15_real(stage_two_3_y15_real),
    .y15_imag(stage_two_3_y15_imag));
  Stage_Three stage_three_3 (
    .x0_real(stage_two_3_y0_real), .x0_imag(stage_two_3_y0_imag), .x1_real(stage_two_3_y1_real),
    .x1_imag(stage_two_3_y1_imag), .x2_real(stage_two_3_y2_real), .x2_imag(stage_two_3_y2_imag),
    .x3_real(stage_two_3_y3_real), .x3_imag(stage_two_3_y3_imag), .x4_real(stage_two_3_y4_real),
    .x4_imag(stage_two_3_y4_imag), .x5_real(stage_two_3_y5_real), .x5_imag(stage_two_3_y5_imag),
    .x6_real(stage_two_3_y6_real), .x6_imag(stage_two_3_y6_imag), .x7_real(stage_two_3_y7_real),
    .x7_imag(stage_two_3_y7_imag), .x8_real(stage_two_3_y8_real), .x8_imag(stage_two_3_y8_imag),
    .x9_real(stage_two_3_y9_real), .x9_imag(stage_two_3_y9_imag), .x10_real(stage_two_3_y10_real),
    .x10_imag(stage_two_3_y10_imag), .x11_real(stage_two_3_y11_real), .x11_imag(stage_two_3_y11_imag),
    .x12_real(stage_two_3_y12_real), .x12_imag(stage_two_3_y12_imag), .x13_real(stage_two_3_y13_real),
    .x13_imag(stage_two_3_y13_imag), .x14_real(stage_two_3_y14_real), .x14_imag(stage_two_3_y14_imag),
    .x15_real(stage_two_3_y15_real), .x15_imag(stage_two_3_y15_imag), .y0_real(stage_three_3_y0_real),
    .y0_imag(stage_three_3_y0_imag), .y1_real(stage_three_3_y1_real), .y1_imag(stage_three_3_y1_imag),
    .y2_real(stage_three_3_y2_real), .y2_imag(stage_three_3_y2_imag), .y3_real(stage_three_3_y3_real),
    .y3_imag(stage_three_3_y3_imag), .y4_real(stage_three_3_y4_real), .y4_imag(stage_three_3_y4_imag),
    .y5_real(stage_three_3_y5_real), .y5_imag(stage_three_3_y5_imag), .y6_real(stage_three_3_y6_real),
    .y6_imag(stage_three_3_y6_imag), .y7_real(stage_three_3_y7_real), .y7_imag(stage_three_3_y7_imag),
    .y8_real(stage_three_3_y8_real), .y8_imag(stage_three_3_y8_imag), .y9_real(stage_three_3_y9_real),
    .y9_imag(stage_three_3_y9_imag), .y10_real(stage_three_3_y10_real), .y10_imag(stage_three_3_y10_imag),
    .y11_real(stage_three_3_y11_real), .y11_imag(stage_three_3_y11_imag), .y12_real(stage_three_3_y12_real),
    .y12_imag(stage_three_3_y12_imag), .y13_real(stage_three_3_y13_real), .y13_imag(stage_three_3_y13_imag),
    .y14_real(stage_three_3_y14_real), .y14_imag(stage_three_3_y14_imag), .y15_real(stage_three_3_y15_real),
    .y15_imag(stage_three_3_y15_imag));
  Stage_Four stage_four_3 (
    .x0_real(stage_three_3_y0_real), .x0_imag(stage_three_3_y0_imag), .x1_real(stage_three_3_y1_real),
    .x1_imag(stage_three_3_y1_imag), .x2_real(stage_three_3_y2_real), .x2_imag(stage_three_3_y2_imag),
    .x3_real(stage_three_3_y3_real), .x3_imag(stage_three_3_y3_imag), .x4_real(stage_three_3_y4_real),
    .x4_imag(stage_three_3_y4_imag), .x5_real(stage_three_3_y5_real), .x5_imag(stage_three_3_y5_imag),
    .x6_real(stage_three_3_y6_real), .x6_imag(stage_three_3_y6_imag), .x7_real(stage_three_3_y7_real),
    .x7_imag(stage_three_3_y7_imag), .x8_real(stage_three_3_y8_real), .x8_imag(stage_three_3_y8_imag),
    .x9_real(stage_three_3_y9_real), .x9_imag(stage_three_3_y9_imag), .x10_real(stage_three_3_y10_real),
    .x10_imag(stage_three_3_y10_imag), .x11_real(stage_three_3_y11_real), .x11_imag(stage_three_3_y11_imag),
    .x12_real(stage_three_3_y12_real), .x12_imag(stage_three_3_y12_imag), .x13_real(stage_three_3_y13_real),
    .x13_imag(stage_three_3_y13_imag), .x14_real(stage_three_3_y14_real), .x14_imag(stage_three_3_y14_imag),
    .x15_real(stage_three_3_y15_real), .x15_imag(stage_three_3_y15_imag), .y0_real(stage_four_3_y0_real),
    .y0_imag(stage_four_3_y0_imag), .y1_real(stage_four_3_y1_real), .y1_imag(stage_four_3_y1_imag),
    .y2_real(stage_four_3_y2_real), .y2_imag(stage_four_3_y2_imag), .y3_real(stage_four_3_y3_real),
    .y3_imag(stage_four_3_y3_imag), .y4_real(stage_four_3_y4_real), .y4_imag(stage_four_3_y4_imag),
    .y5_real(stage_four_3_y5_real), .y5_imag(stage_four_3_y5_imag), .y6_real(stage_four_3_y6_real),
    .y6_imag(stage_four_3_y6_imag), .y7_real(stage_four_3_y7_real), .y7_imag(stage_four_3_y7_imag),
    .y8_real(stage_four_3_y8_real), .y8_imag(stage_four_3_y8_imag), .y9_real(stage_four_3_y9_real),
    .y9_imag(stage_four_3_y9_imag), .y10_real(stage_four_3_y10_real), .y10_imag(stage_four_3_y10_imag),
    .y11_real(stage_four_3_y11_real), .y11_imag(stage_four_3_y11_imag), .y12_real(stage_four_3_y12_real),
    .y12_imag(stage_four_3_y12_imag), .y13_real(stage_four_3_y13_real), .y13_imag(stage_four_3_y13_imag),
    .y14_real(stage_four_3_y14_real), .y14_imag(stage_four_3_y14_imag), .y15_real(stage_four_3_y15_real));  // open: y15_imag
  // Probe on stage_four_3_y9_real
  // Probe on stage_four_3_y10_real
  // Probe on stage_four_3_y11_real
  // Probe on stage_four_3_y12_real
  // Probe on stage_four_3_y13_real
  // Probe on stage_four_3_y0_real
  // Probe on stage_four_3_y1_real
  // Probe on stage_four_3_y2_real
  // Probe on stage_four_3_y3_real
  // Probe on stage_four_3_y4_real
  // Probe on stage_four_3_y5_real
  // Probe on stage_four_3_y6_real
  // Probe on stage_four_3_y7_real
  // Probe on stage_four_3_y8_real
  // Probe on stage_four_3_y14_real
  // Probe on stage_four_3_y15_real

  // Notes on the sheet:
  //   Constant -> Impulse
  //    Impulse ->  Constant
  //   Cosine(2 * pi * 4 *t) -> Impulses at k =4 and 12
endmodule

module Add_Sub_Shift (
  input  [15:0] X_real,
  input  [15:0] X_imag,
  input  [15:0] Y_real,
  input  [15:0] Y_imag,
  output [15:0] Sum_Real,
  output [15:0] Sum_imag,
  output [15:0] Dif_Real,
  output [15:0] Dif_imag
);

  wire [16:0] adder_1_out, adder_2_out, bit_extender_1_out, bit_extender_2_out, bit_extender_3_out,
       bit_extender_4_out, bit_extender_5_out, bit_extender_6_out, bit_extender_7_out, bit_extender_8_out,
       subtractor_1_out, subtractor_2_out;
  wire [16:16] shifter_1_out, shifter_2_out, shifter_3_out, shifter_4_out;

  // Probe on X_real
  assign bit_extender_1_out = {{1{X_real[15]}}, X_real};  // Bit_Extender bit_extender_1
  assign bit_extender_2_out = {{1{Y_real[15]}}, Y_real};  // Bit_Extender bit_extender_2
  // Probe on Y_real
  assign bit_extender_3_out = {{1{X_imag[15]}}, X_imag};  // Bit_Extender bit_extender_3
  assign bit_extender_4_out = {{1{Y_imag[15]}}, Y_imag};  // Bit_Extender bit_extender_4
  // Probe on X_real
  assign bit_extender_5_out = {{1{X_real[15]}}, X_real};  // Bit_Extender bit_extender_5
  assign bit_extender_6_out = {{1{Y_real[15]}}, Y_real};  // Bit_Extender bit_extender_6
  // Probe on Y_real
  assign bit_extender_7_out = {{1{X_imag[15]}}, X_imag};  // Bit_Extender bit_extender_7
  assign bit_extender_8_out = {{1{Y_imag[15]}}, Y_imag};  // Bit_Extender bit_extender_8
  Adder #(.width(17)) adder_1 (.a(bit_extender_1_out), .b(bit_extender_2_out), .out(adder_1_out));  // open: cin, cout
  Subtractor #(.width(17)) subtractor_1 (
    .a(bit_extender_5_out), .b(bit_extender_6_out), .out(subtractor_1_out));  // open: bin, bout
  Subtractor #(.width(17)) subtractor_2 (
    .a(bit_extender_7_out), .b(bit_extender_8_out), .out(subtractor_2_out));  // open: bin, bout
  Shifter #(.width(17), .shift("ar")) shifter_1 (
    .in(adder_1_out), .\dist (5'b00001), .out({shifter_1_out[16], Sum_Real}));
  Adder #(.width(17)) adder_2 (.a(bit_extender_3_out), .b(bit_extender_4_out), .out(adder_2_out));  // open: cin, cout
  Shifter #(.width(17), .shift("ar")) shifter_2 (
    .in(adder_2_out), .\dist (5'b00001), .out({shifter_2_out[16], Sum_imag}));
  Shifter #(.width(17), .shift("ar")) shifter_3 (
    .in(subtractor_1_out), .\dist (5'b00001), .out({shifter_3_out[16], Dif_Real}));
  Shifter #(.width(17), .shift("ar")) shifter_4 (
    .in(subtractor_2_out), .\dist (5'b00001), .out({shifter_4_out[16], Dif_imag}));
  // Probe on Sum_Real
  // Probe on Dif_Real

  // Other names for the same wires on the sheet: xi[15:0] = X_imag; xr[15:0] = X_real; yi[15:0] = Y_imag;
  //   yr[15:0] = Y_real
endmodule

module Add (
  input  [15:0] X_real,
  input  [15:0] X_imag,
  input  [15:0] Y_real,
  input  [15:0] Y_imag,
  output [15:0] Sum_Real,
  output [15:0] Sum_imag
);

  wire [16:0] bit_extender_1_out, bit_extender_2_out, bit_extender_3_out, bit_extender_4_out;
  wire [16:16] adder_1_out, adder_2_out;

  // Probe on X_real
  assign bit_extender_1_out = {{1{X_real[15]}}, X_real};  // Bit_Extender bit_extender_1
  assign bit_extender_2_out = {{1{Y_real[15]}}, Y_real};  // Bit_Extender bit_extender_2
  // Probe on Y_real
  Adder #(.width(17)) adder_1 (
    .a(bit_extender_1_out), .b(bit_extender_2_out), .out({adder_1_out[16], Sum_Real}));  // open: cin, cout
  Shifter #(.width(17), .shift("ar")) shifter_1 ();  // open: in, dist, out
  // Probe on Sum_Real
  assign bit_extender_3_out = {{1{X_imag[15]}}, X_imag};  // Bit_Extender bit_extender_3
  assign bit_extender_4_out = {{1{Y_imag[15]}}, Y_imag};  // Bit_Extender bit_extender_4
  Adder #(.width(17)) adder_2 (
    .a(bit_extender_3_out), .b(bit_extender_4_out), .out({adder_2_out[16], Sum_imag}));  // open: cin, cout

  // Notes on the sheet:
  //   Adds two complex numbers in Q1.15 format
endmodule

module Sub (
  input  [15:0] X_real,
  input  [15:0] X_imag,
  input  [15:0] Y_real,
  input  [15:0] Y_imag,
  output [15:0] Dif_Real,
  output [15:0] Dif_imag
);

  wire [16:0] bit_extender_1_out, bit_extender_2_out, bit_extender_3_out, bit_extender_4_out,
       subtractor_1_out, subtractor_2_out;
  wire [16:16] shifter_1_out, shifter_2_out;

  // Probe on X_real
  // Probe on Y_real
  assign bit_extender_1_out = {{1{X_real[15]}}, X_real};  // Bit_Extender bit_extender_1
  assign bit_extender_2_out = {{1{Y_real[15]}}, Y_real};  // Bit_Extender bit_extender_2
  Subtractor #(.width(17)) subtractor_1 (
    .a(bit_extender_1_out), .b(bit_extender_2_out), .out(subtractor_1_out));  // open: bin, bout
  Shifter #(.width(17), .shift("ar")) shifter_1 (
    .in(subtractor_1_out), .\dist (5'b00001), .out({shifter_1_out[16], Dif_Real}));
  // Probe on Dif_Real
  assign bit_extender_3_out = {{1{X_imag[15]}}, X_imag};  // Bit_Extender bit_extender_3
  assign bit_extender_4_out = {{1{Y_imag[15]}}, Y_imag};  // Bit_Extender bit_extender_4
  Subtractor #(.width(17)) subtractor_2 (
    .a(bit_extender_3_out), .b(bit_extender_4_out), .out(subtractor_2_out));  // open: bin, bout
  Shifter #(.width(17), .shift("ar")) shifter_2 (
    .in(subtractor_2_out), .\dist (5'b00001), .out({shifter_2_out[16], Dif_imag}));

  // Notes on the sheet:
  //   Subtracts two numbers in Q1.15 format
endmodule

module Mult (
  input  [15:0] A_real,
  input  [15:0] B_real,
  input  [15:0] A_imag,
  input  [15:0] B_imag,
  output [15:0] AxB_real,
  output [15:0] AxB_imag
);

  wire xor_1_out, xor_2_out, xor_3_out, xor_4_out;
  wire [15:0] Ai_x_Bi, Ai_x_Br, Ar_x_Bi, Ar_x_Br, multiplexer_1_out, multiplexer_2_out, multiplexer_3_out,
       multiplexer_4_out, multiplexer_5_out, multiplexer_6_out, multiplexer_7_out, multiplexer_8_out,
       multiplier_1_cout, multiplier_1_out, multiplier_2_cout, multiplier_2_out, multiplier_3_cout,
       multiplier_3_out, multiplier_4_cout, multiplier_4_out, negator_1_out, negator_2_out, negator_3_out,
       negator_4_out, negator_5_out, negator_6_out, negator_7_out, negator_8_out;
  wire [31:0] multiplexer_9_out, multiplexer_10_out, multiplexer_11_out, multiplexer_12_out, negator_9_out,
       negator_10_out, negator_11_out, negator_12_out;
  wire [31:16] shifter_1_out, shifter_2_out, shifter_3_out, shifter_4_out;

  // Probe on A_real
  // Probe on B_real
  // Probe on A_imag
  // Probe on B_imag
  // Probe on A_real
  // Probe on B_imag
  // Probe on A_imag
  // Probe on B_real
  Negator #(.width(16)) negator_1 (.in(A_real), .out(negator_1_out));
  Negator #(.width(16)) negator_2 (.in(B_real), .out(negator_2_out));
  Negator #(.width(16)) negator_3 (.in(A_imag), .out(negator_3_out));
  Negator #(.width(16)) negator_4 (.in(B_imag), .out(negator_4_out));
  Negator #(.width(16)) negator_5 (.in(A_real), .out(negator_5_out));
  Negator #(.width(16)) negator_6 (.in(B_imag), .out(negator_6_out));
  Negator #(.width(16)) negator_7 (.in(A_imag), .out(negator_7_out));
  Negator #(.width(16)) negator_8 (.in(B_real), .out(negator_8_out));
  Multiplexer #(.width(16), .enable("false")) multiplexer_1 (
    .in0(A_real), .in1(negator_1_out), .out(multiplexer_1_out), .sel(A_real[15]));
  Multiplexer #(.width(16), .enable("false")) multiplexer_2 (
    .in0(B_real), .in1(negator_2_out), .out(multiplexer_2_out), .sel(B_real[15]));
  Multiplexer #(.width(16), .enable("false")) multiplexer_3 (
    .in0(A_imag), .in1(negator_3_out), .out(multiplexer_3_out), .sel(A_imag[15]));
  Multiplexer #(.width(16), .enable("false")) multiplexer_4 (
    .in0(B_imag), .in1(negator_4_out), .out(multiplexer_4_out), .sel(B_imag[15]));
  Multiplexer #(.width(16), .enable("false")) multiplexer_5 (
    .in0(A_real), .in1(negator_5_out), .out(multiplexer_5_out), .sel(A_real[15]));
  Multiplexer #(.width(16), .enable("false")) multiplexer_6 (
    .in0(B_imag), .in1(negator_6_out), .out(multiplexer_6_out), .sel(B_imag[15]));
  Multiplexer #(.width(16), .enable("false")) multiplexer_7 (
    .in0(A_imag), .in1(negator_7_out), .out(multiplexer_7_out), .sel(A_imag[15]));
  Multiplexer #(.width(16), .enable("false")) multiplexer_8 (
    .in0(B_real), .in1(negator_8_out), .out(multiplexer_8_out), .sel(B_real[15]));
  Multiplier #(.width(16)) multiplier_1 (
    .a(multiplexer_1_out), .b(multiplexer_2_out), .out(multiplier_1_out), .cout(multiplier_1_cout));  // open: cin
  Multiplier #(.width(16)) multiplier_2 (
    .a(multiplexer_3_out), .b(multiplexer_4_out), .out(multiplier_2_out), .cout(multiplier_2_cout));  // open: cin
  Multiplier #(.width(16)) multiplier_3 (
    .a(multiplexer_5_out), .b(multiplexer_6_out), .out(multiplier_3_out), .cout(multiplier_3_cout));  // open: cin
  Multiplier #(.width(16)) multiplier_4 (
    .a(multiplexer_7_out), .b(multiplexer_8_out), .out(multiplier_4_out), .cout(multiplier_4_cout));  // open: cin
  Negator #(.width(32)) negator_9 (.in({multiplier_1_cout, multiplier_1_out}), .out(negator_9_out));
  Negator #(.width(32)) negator_10 (.in({multiplier_2_cout, multiplier_2_out}), .out(negator_10_out));
  Negator #(.width(32)) negator_11 (.in({multiplier_3_cout, multiplier_3_out}), .out(negator_11_out));
  Negator #(.width(32)) negator_12 (.in({multiplier_4_cout, multiplier_4_out}), .out(negator_12_out));
  Multiplexer #(.width(32), .enable("false")) multiplexer_9 (
    .in0({multiplier_1_cout, multiplier_1_out}), .in1(negator_9_out), .out(multiplexer_9_out), .sel(xor_1_out));
  xor xor_1 (xor_1_out, A_real[15], B_real[15]);
  Multiplexer #(.width(32), .enable("false")) multiplexer_10 (
    .in0(negator_10_out), .in1({multiplier_2_cout, multiplier_2_out}), .out(multiplexer_10_out),
    .sel(xor_2_out));
  xor xor_2 (xor_2_out, A_imag[15], B_imag[15]);
  Multiplexer #(.width(32), .enable("false")) multiplexer_11 (
    .in0({multiplier_3_cout, multiplier_3_out}), .in1(negator_11_out), .out(multiplexer_11_out),
    .sel(xor_3_out));
  xor xor_3 (xor_3_out, A_real[15], B_imag[15]);
  Multiplexer #(.width(32), .enable("false")) multiplexer_12 (
    .in0({multiplier_4_cout, multiplier_4_out}), .in1(negator_12_out), .out(multiplexer_12_out),
    .sel(xor_4_out));
  xor xor_4 (xor_4_out, A_imag[15], B_real[15]);
  // Probe on multiplexer_9_out
  Shifter #(.width(32), .shift("ar")) shifter_1 (
    .in(multiplexer_9_out), .\dist (5'b01111), .out({shifter_1_out, Ar_x_Br}));
  // Probe on multiplexer_10_out
  // Probe on multiplexer_11_out
  // Probe on multiplexer_12_out
  Shifter #(.width(32), .shift("ar")) shifter_2 (
    .in(multiplexer_12_out), .\dist (5'b01111), .out({shifter_2_out, Ai_x_Br}));
  Shifter #(.width(32), .shift("ar")) shifter_3 (
    .in(multiplexer_10_out), .\dist (5'b01111), .out({shifter_3_out, Ai_x_Bi}));
  Shifter #(.width(32), .shift("ar")) shifter_4 (
    .in(multiplexer_11_out), .\dist (5'b01111), .out({shifter_4_out, Ar_x_Bi}));
  // Probe on AxB_real
  Add add_1 (.X_real(Ar_x_Br), .Y_real(Ai_x_Bi), .Sum_Real(AxB_real));  // open: X_imag, Y_imag, Sum_imag
  Add add_2 (.X_imag(Ai_x_Br), .Y_imag(Ar_x_Bi), .Sum_imag(AxB_imag));  // open: X_real, Y_real, Sum_Real
  // Probe on AxB_imag

  // Other names for the same wires on the sheet: Xi[15:0] = A_imag; MSB_X_I = A_imag[15]; Xr[15:0] = A_real;
  //   MSB_X_R = A_real[15]; Yi[15:0] = B_imag; MSB_Y_I = B_imag[15]; Yr[15:0] = B_real; MSB_Y_R = B_real[15]

  // Notes on the sheet:
  //   Multiplies two numbers in Q1.15 format
endmodule

module Stage_One (
  input  [15:0] x0_real,
  input  [15:0] x0_imag,
  input  [15:0] x1_real,
  input  [15:0] x1_imag,
  input  [15:0] x2_real,
  input  [15:0] x2_imag,
  input  [15:0] x3_real,
  input  [15:0] x3_imag,
  input  [15:0] x4_real,
  input  [15:0] x4_imag,
  input  [15:0] x5_real,
  input  [15:0] x5_imag,
  input  [15:0] x6_real,
  input  [15:0] x6_imag,
  input  [15:0] x7_real,
  input  [15:0] x7_imag,
  input  [15:0] x8_real,
  input  [15:0] x8_imag,
  input  [15:0] x9_real,
  input  [15:0] x9_imag,
  input  [15:0] x10_real,
  input  [15:0] x10_imag,
  input  [15:0] x11_real,
  input  [15:0] x11_imag,
  input  [15:0] x12_real,
  input  [15:0] x12_imag,
  input  [15:0] x13_real,
  input  [15:0] x13_imag,
  input  [15:0] x14_real,
  input  [15:0] x14_imag,
  input  [15:0] x15_real,
  input  [15:0] x15_imag,
  output [15:0] y0_real,
  output [15:0] y0_imag,
  output [15:0] y1_real,
  output [15:0] y1_imag,
  output [15:0] y2_real,
  output [15:0] y2_imag,
  output [15:0] y3_real,
  output [15:0] y3_imag,
  output [15:0] y4_real,
  output [15:0] y4_imag,
  output [15:0] y5_real,
  output [15:0] y5_imag,
  output [15:0] y6_real,
  output [15:0] y6_imag,
  output [15:0] y7_real,
  output [15:0] y7_imag,
  output [15:0] y8_real,
  output [15:0] y8_imag,
  output [15:0] y9_real,
  output [15:0] y9_imag,
  output [15:0] y10_real,
  output [15:0] y10_imag,
  output [15:0] y11_real,
  output [15:0] y11_imag,
  output [15:0] y12_real,
  output [15:0] y12_imag,
  output [15:0] y13_real,
  output [15:0] y13_imag,
  output [15:0] y14_real,
  output [15:0] y14_imag,
  output [15:0] y15_real,
  output [15:0] y15_imag
);

  Add_Sub_Shift add_sub_shift_1 (
    .X_real(x0_real), .X_imag(x0_imag), .Y_real(x8_real), .Y_imag(x8_imag), .Sum_Real(y0_real),
    .Sum_imag(y0_imag), .Dif_Real(y1_real), .Dif_imag(y1_imag));
  Add_Sub_Shift add_sub_shift_2 (
    .X_real(x4_real), .X_imag(x4_imag), .Y_real(x12_real), .Y_imag(x12_imag), .Sum_Real(y2_real),
    .Sum_imag(y2_imag), .Dif_Real(y3_real), .Dif_imag(y3_imag));
  Add_Sub_Shift add_sub_shift_3 (
    .X_real(x2_real), .X_imag(x2_imag), .Y_real(x10_real), .Y_imag(x10_imag), .Sum_Real(y4_real),
    .Sum_imag(y4_imag), .Dif_Real(y5_real), .Dif_imag(y5_imag));
  Add_Sub_Shift add_sub_shift_4 (
    .X_real(x6_real), .X_imag(x6_imag), .Y_real(x14_real), .Y_imag(x14_imag), .Sum_Real(y6_real),
    .Sum_imag(y6_imag), .Dif_Real(y7_real), .Dif_imag(y7_imag));
  Add_Sub_Shift add_sub_shift_5 (
    .X_real(x1_real), .X_imag(x1_imag), .Y_real(x9_real), .Y_imag(x9_imag), .Sum_Real(y8_real),
    .Sum_imag(y8_imag), .Dif_Real(y9_real), .Dif_imag(y9_imag));
  Add_Sub_Shift add_sub_shift_6 (
    .X_real(x5_real), .X_imag(x5_imag), .Y_real(x13_real), .Y_imag(x13_imag), .Sum_Real(y10_real),
    .Sum_imag(y10_imag), .Dif_Real(y11_real), .Dif_imag(y11_imag));
  Add_Sub_Shift add_sub_shift_7 (
    .X_real(x3_real), .X_imag(x3_imag), .Y_real(x11_real), .Y_imag(x11_imag), .Sum_Real(y12_real),
    .Sum_imag(y12_imag), .Dif_Real(y13_real), .Dif_imag(y13_imag));
  Add_Sub_Shift add_sub_shift_8 (
    .X_real(x7_real), .X_imag(x7_imag), .Y_real(x15_real), .Y_imag(x15_imag), .Sum_Real(y14_real),
    .Sum_imag(y14_imag), .Dif_Real(y15_real), .Dif_imag(y15_imag));

  // Other names for the same wires on the sheet: x0i[15:0] = x0_imag; x0r[15:0] = x0_real; x1i[15:0] = x1_imag;
  //   x1r[15:0] = x1_real; x2i[15:0] = x2_imag; x2r[15:0] = x2_real; x3i[15:0] = x3_imag; x3r[15:0] = x3_real;
  //   x4i[15:0] = x4_imag; x4r[15:0] = x4_real; x5i[15:0] = x5_imag; x5r[15:0] = x5_real; x6i[15:0] = x6_imag;
  //   x6r[15:0] = x6_real; x7i[15:0] = x7_imag; x7r[15:0] = x7_real; x8i[15:0] = x8_imag; x8r[15:0] = x8_real;
  //   x9i[15:0] = x9_imag; x9r[15:0] = x9_real; x10i[15:0] = x10_imag; x10r[15:0] = x10_real; x11i[15:0] = x11_imag;
  //   x11r[15:0] = x11_real; x12i[15:0] = x12_imag; x12r[15:0] = x12_real; x13i[15:0] = x13_imag;
  //   x13r[15:0] = x13_real; x14i[15:0] = x14_imag; x14r[15:0] = x14_real; x15i[15:0] = x15_imag;
  //   x15r[15:0] = x15_real; y0i[15:0] = y0_imag; y0r[15:0] = y0_real; y1i[15:0] = y1_imag; y1r[15:0] = y1_real;
  //   y2i[15:0] = y2_imag; y2r[15:0] = y2_real; y3i[15:0] = y3_imag; y3r[15:0] = y3_real; y4i[15:0] = y4_imag;
  //   y4r[15:0] = y4_real; y5i[15:0] = y5_imag; y5r[15:0] = y5_real; y6i[15:0] = y6_imag; y6r[15:0] = y6_real;
  //   y7i[15:0] = y7_imag; y7r[15:0] = y7_real; y8i[15:0] = y8_imag; y8r[15:0] = y8_real; y9i[15:0] = y9_imag;
  //   y9r[15:0] = y9_real; y10i[15:0] = y10_imag; y10r[15:0] = y10_real; y11i[15:0] = y11_imag; y11r[15:0] = y11_real;
  //   y12i[15:0] = y12_imag; y12r[15:0] = y12_real; y13i[15:0] = y13_imag; y13r[15:0] = y13_real;
  //   y14i[15:0] = y14_imag; y14r[15:0] = y14_real; y15i[15:0] = y15_imag; y15r[15:0] = y15_real

  // Notes on the sheet:
  //   Stage One
  //   8 groups of size two FFT
  //   each group consists of one butterfly
  //   mixing x_i with x_i+8
endmodule

module Stage_Two (
  input  [15:0] x0_real,
  input  [15:0] x0_imag,
  input  [15:0] x1_real,
  input  [15:0] x1_imag,
  input  [15:0] x2_real,
  input  [15:0] x2_imag,
  input  [15:0] x3_real,
  input  [15:0] x3_imag,
  input  [15:0] x4_real,
  input  [15:0] x4_imag,
  input  [15:0] x5_real,
  input  [15:0] x5_imag,
  input  [15:0] x6_real,
  input  [15:0] x6_imag,
  input  [15:0] x7_real,
  input  [15:0] x7_imag,
  input  [15:0] x8_real,
  input  [15:0] x8_imag,
  input  [15:0] x9_real,
  input  [15:0] x9_imag,
  input  [15:0] x10_real,
  input  [15:0] x10_imag,
  input  [15:0] x11_real,
  input  [15:0] x11_imag,
  input  [15:0] x12_real,
  input  [15:0] x12_imag,
  input  [15:0] x13_real,
  input  [15:0] x13_imag,
  input  [15:0] x14_real,
  input  [15:0] x14_imag,
  input  [15:0] x15_real,
  input  [15:0] x15_imag,
  output [15:0] y0_real,
  output [15:0] y0_imag,
  output [15:0] y1_real,
  output [15:0] y1_imag,
  output [15:0] y2_real,
  output [15:0] y2_imag,
  output [15:0] y3_real,
  output [15:0] y3_imag,
  output [15:0] y4_real,
  output [15:0] y4_imag,
  output [15:0] y5_real,
  output [15:0] y5_imag,
  output [15:0] y6_real,
  output [15:0] y6_imag,
  output [15:0] y7_real,
  output [15:0] y7_imag,
  output [15:0] y8_real,
  output [15:0] y8_imag,
  output [15:0] y9_real,
  output [15:0] y9_imag,
  output [15:0] y10_real,
  output [15:0] y10_imag,
  output [15:0] y11_real,
  output [15:0] y11_imag,
  output [15:0] y12_real,
  output [15:0] y12_imag,
  output [15:0] y13_real,
  output [15:0] y13_imag,
  output [15:0] y14_real,
  output [15:0] y14_imag,
  output [15:0] y15_real,
  output [15:0] y15_imag
);

  wire [15:0] negator_1_out, negator_2_out, negator_3_out, negator_4_out;

  Negator #(.width(16)) negator_1 (.in(x3_real), .out(negator_1_out));
  Negator #(.width(16)) negator_2 (.in(x7_real), .out(negator_2_out));
  Negator #(.width(16)) negator_3 (.in(x11_real), .out(negator_3_out));
  Negator #(.width(16)) negator_4 (.in(x15_real), .out(negator_4_out));
  Add_Sub_Shift add_sub_shift_1 (
    .X_real(x0_real), .X_imag(x0_imag), .Y_real(x2_real), .Y_imag(x2_imag), .Sum_Real(y0_real),
    .Sum_imag(y0_imag), .Dif_Real(y2_real), .Dif_imag(y2_imag));
  Add_Sub_Shift add_sub_shift_2 (
    .X_real(x1_real), .X_imag(x1_imag), .Y_real(x3_imag), .Y_imag(negator_1_out), .Sum_Real(y1_real),
    .Sum_imag(y1_imag), .Dif_Real(y3_real), .Dif_imag(y3_imag));
  Add_Sub_Shift add_sub_shift_3 (
    .X_real(x4_real), .X_imag(x4_imag), .Y_real(x6_real), .Y_imag(x6_imag), .Sum_Real(y4_real),
    .Sum_imag(y4_imag), .Dif_Real(y6_real), .Dif_imag(y6_imag));
  Add_Sub_Shift add_sub_shift_4 (
    .X_real(x5_real), .X_imag(x5_imag), .Y_real(x7_imag), .Y_imag(negator_2_out), .Sum_Real(y5_real),
    .Sum_imag(y5_imag), .Dif_Real(y7_real), .Dif_imag(y7_imag));
  Add_Sub_Shift add_sub_shift_5 (
    .X_real(x8_real), .X_imag(x8_imag), .Y_real(x10_real), .Y_imag(x10_imag), .Sum_Real(y8_real),
    .Sum_imag(y8_imag), .Dif_Real(y10_real), .Dif_imag(y10_imag));
  Add_Sub_Shift add_sub_shift_6 (
    .X_real(x9_real), .X_imag(x9_imag), .Y_real(x11_imag), .Y_imag(negator_3_out), .Sum_Real(y9_real),
    .Sum_imag(y9_imag), .Dif_Real(y11_real), .Dif_imag(y11_imag));
  Add_Sub_Shift add_sub_shift_7 (
    .X_real(x12_real), .X_imag(x12_imag), .Y_real(x14_real), .Y_imag(x14_imag), .Sum_Real(y12_real),
    .Sum_imag(y12_imag), .Dif_Real(y14_real), .Dif_imag(y14_imag));
  Add_Sub_Shift add_sub_shift_8 (
    .X_real(x13_real), .X_imag(x13_imag), .Y_real(x15_imag), .Y_imag(negator_4_out), .Sum_Real(y13_real),
    .Sum_imag(y13_imag), .Dif_Real(y15_real), .Dif_imag(y15_imag));

  // Other names for the same wires on the sheet: x0i[15:0] = x0_imag; x0r[15:0] = x0_real; x1i[15:0] = x1_imag;
  //   x1r[15:0] = x1_real; x2i[15:0] = x2_imag; x2r[15:0] = x2_real; x3i[15:0] = x3_imag; x3r[15:0] = x3_real;
  //   x4i[15:0] = x4_imag; x4r[15:0] = x4_real; x5i[15:0] = x5_imag; x5r[15:0] = x5_real; x6i[15:0] = x6_imag;
  //   x6r[15:0] = x6_real; x7i[15:0] = x7_imag; x7r[15:0] = x7_real; x8i[15:0] = x8_imag; x8r[15:0] = x8_real;
  //   x9i[15:0] = x9_imag; x9r[15:0] = x9_real; x10i[15:0] = x10_imag; x10r[15:0] = x10_real; x11i[15:0] = x11_imag;
  //   x11r[15:0] = x11_real; x12i[15:0] = x12_imag; x12r[15:0] = x12_real; x13i[15:0] = x13_imag;
  //   x13r[15:0] = x13_real; x14i[15:0] = x14_imag; x14r[15:0] = x14_real; x15i[15:0] = x15_imag;
  //   x15r[15:0] = x15_real; y0i[15:0] = y0_imag; y0r[15:0] = y0_real; y1i[15:0] = y1_imag; y1r[15:0] = y1_real;
  //   y2i[15:0] = y2_imag; y2r[15:0] = y2_real; y3i[15:0] = y3_imag; y3r[15:0] = y3_real; y4i[15:0] = y4_imag;
  //   y4r[15:0] = y4_real; y5i[15:0] = y5_imag; y5r[15:0] = y5_real; y6i[15:0] = y6_imag; y6r[15:0] = y6_real;
  //   y7i[15:0] = y7_imag; y7r[15:0] = y7_real; y8i[15:0] = y8_imag; y8r[15:0] = y8_real; y9i[15:0] = y9_imag;
  //   y9r[15:0] = y9_real; y10i[15:0] = y10_imag; y10r[15:0] = y10_real; y11i[15:0] = y11_imag; y11r[15:0] = y11_real;
  //   y12i[15:0] = y12_imag; y12r[15:0] = y12_real; y13i[15:0] = y13_imag; y13r[15:0] = y13_real;
  //   y14i[15:0] = y14_imag; y14r[15:0] = y14_real; y15i[15:0] = y15_imag; y15r[15:0] = y15_real

  // Notes on the sheet:
  //   Stage Two
  //   4 groups of size four FFT
  //   each group consists of two butterfies
  //   mixing x_i with x_i+2
endmodule

module Stage_Three (
  input  [15:0] x0_real,
  input  [15:0] x0_imag,
  input  [15:0] x1_real,
  input  [15:0] x1_imag,
  input  [15:0] x2_real,
  input  [15:0] x2_imag,
  input  [15:0] x3_real,
  input  [15:0] x3_imag,
  input  [15:0] x4_real,
  input  [15:0] x4_imag,
  input  [15:0] x5_real,
  input  [15:0] x5_imag,
  input  [15:0] x6_real,
  input  [15:0] x6_imag,
  input  [15:0] x7_real,
  input  [15:0] x7_imag,
  input  [15:0] x8_real,
  input  [15:0] x8_imag,
  input  [15:0] x9_real,
  input  [15:0] x9_imag,
  input  [15:0] x10_real,
  input  [15:0] x10_imag,
  input  [15:0] x11_real,
  input  [15:0] x11_imag,
  input  [15:0] x12_real,
  input  [15:0] x12_imag,
  input  [15:0] x13_real,
  input  [15:0] x13_imag,
  input  [15:0] x14_real,
  input  [15:0] x14_imag,
  input  [15:0] x15_real,
  input  [15:0] x15_imag,
  output [15:0] y0_real,
  output [15:0] y0_imag,
  output [15:0] y1_real,
  output [15:0] y1_imag,
  output [15:0] y2_real,
  output [15:0] y2_imag,
  output [15:0] y3_real,
  output [15:0] y3_imag,
  output [15:0] y4_real,
  output [15:0] y4_imag,
  output [15:0] y5_real,
  output [15:0] y5_imag,
  output [15:0] y6_real,
  output [15:0] y6_imag,
  output [15:0] y7_real,
  output [15:0] y7_imag,
  output [15:0] y8_real,
  output [15:0] y8_imag,
  output [15:0] y9_real,
  output [15:0] y9_imag,
  output [15:0] y10_real,
  output [15:0] y10_imag,
  output [15:0] y11_real,
  output [15:0] y11_imag,
  output [15:0] y12_real,
  output [15:0] y12_imag,
  output [15:0] y13_real,
  output [15:0] y13_imag,
  output [15:0] y14_real,
  output [15:0] y14_imag,
  output [15:0] y15_real,
  output [15:0] y15_imag
);

  wire [15:0] mult_1_axb_imag, mult_1_axb_real, mult_2_axb_imag, mult_2_axb_real, mult_3_axb_imag,
       mult_3_axb_real, mult_4_axb_imag, mult_4_axb_real, negator_1_out, negator_2_out;

  Mult mult_1 (
    .A_real(x5_real), .B_real(16'h5a82), .A_imag(x5_imag), .B_imag(16'ha57e), .AxB_real(mult_1_axb_real),
    .AxB_imag(mult_1_axb_imag));
  Negator #(.width(16)) negator_1 (.in(x6_real), .out(negator_1_out));
  Mult mult_2 (
    .A_real(x7_real), .B_real(16'ha57e), .A_imag(x7_imag), .B_imag(16'ha57e), .AxB_real(mult_2_axb_real),
    .AxB_imag(mult_2_axb_imag));
  Mult mult_3 (
    .A_real(x13_real), .B_real(16'h5a82), .A_imag(x13_imag), .B_imag(16'ha57e), .AxB_real(mult_3_axb_real),
    .AxB_imag(mult_3_axb_imag));
  Negator #(.width(16)) negator_2 (.in(x14_real), .out(negator_2_out));
  Mult mult_4 (
    .A_real(x15_real), .B_real(16'ha57e), .A_imag(x15_imag), .B_imag(16'ha57e), .AxB_real(mult_4_axb_real),
    .AxB_imag(mult_4_axb_imag));
  Add_Sub_Shift add_sub_shift_1 (
    .X_real(x0_real), .X_imag(x0_imag), .Y_real(x4_real), .Y_imag(x4_imag), .Sum_Real(y0_real),
    .Sum_imag(y0_imag), .Dif_Real(y4_real), .Dif_imag(y4_imag));
  Add_Sub_Shift add_sub_shift_2 (
    .X_real(x1_real), .X_imag(x1_imag), .Y_real(mult_1_axb_real), .Y_imag(mult_1_axb_imag),
    .Sum_Real(y1_real), .Sum_imag(y1_imag), .Dif_Real(y5_real), .Dif_imag(y5_imag));
  Add_Sub_Shift add_sub_shift_3 (
    .X_real(x2_real), .X_imag(x2_imag), .Y_real(x6_imag), .Y_imag(negator_1_out), .Sum_Real(y2_real),
    .Sum_imag(y2_imag), .Dif_Real(y6_real), .Dif_imag(y6_imag));
  Add_Sub_Shift add_sub_shift_4 (
    .X_real(x3_real), .X_imag(x3_imag), .Y_real(mult_2_axb_real), .Y_imag(mult_2_axb_imag),
    .Sum_Real(y3_real), .Sum_imag(y3_imag), .Dif_Real(y7_real), .Dif_imag(y7_imag));
  Add_Sub_Shift add_sub_shift_5 (
    .X_real(x8_real), .X_imag(x8_imag), .Y_real(x12_real), .Y_imag(x12_imag), .Sum_Real(y8_real),
    .Sum_imag(y8_imag), .Dif_Real(y12_real), .Dif_imag(y12_imag));
  Add_Sub_Shift add_sub_shift_6 (
    .X_real(x9_real), .X_imag(x9_imag), .Y_real(mult_3_axb_real), .Y_imag(mult_3_axb_imag),
    .Sum_Real(y9_real), .Sum_imag(y9_imag), .Dif_Real(y13_real), .Dif_imag(y13_imag));
  Add_Sub_Shift add_sub_shift_7 (
    .X_real(x10_real), .X_imag(x10_imag), .Y_real(x14_imag), .Y_imag(negator_2_out), .Sum_Real(y10_real),
    .Sum_imag(y10_imag), .Dif_Real(y14_real), .Dif_imag(y14_imag));
  Add_Sub_Shift add_sub_shift_8 (
    .X_real(x11_real), .X_imag(x11_imag), .Y_real(mult_4_axb_real), .Y_imag(mult_4_axb_imag),
    .Sum_Real(y11_real), .Sum_imag(y11_imag), .Dif_Real(y15_real), .Dif_imag(y15_imag));

  // Other names for the same wires on the sheet: x0i[15:0] = x0_imag; x0r[15:0] = x0_real; x1i[15:0] = x1_imag;
  //   x1r[15:0] = x1_real; x2i[15:0] = x2_imag; x2r[15:0] = x2_real; x3i[15:0] = x3_imag; x3r[15:0] = x3_real;
  //   x4i[15:0] = x4_imag; x4r[15:0] = x4_real; x5i[15:0] = x5_imag; x5r[15:0] = x5_real; x6i[15:0] = x6_imag;
  //   x6r[15:0] = x6_real; x7i[15:0] = x7_imag; x7r[15:0] = x7_real; x8i[15:0] = x8_imag; x8r[15:0] = x8_real;
  //   x9i[15:0] = x9_imag; x9r[15:0] = x9_real; x10i[15:0] = x10_imag; x10r[15:0] = x10_real; x11i[15:0] = x11_imag;
  //   x11r[15:0] = x11_real; x12i[15:0] = x12_imag; x12r[15:0] = x12_real; x13i[15:0] = x13_imag;
  //   x13r[15:0] = x13_real; x14i[15:0] = x14_imag; x14r[15:0] = x14_real; x15i[15:0] = x15_imag;
  //   x15r[15:0] = x15_real; y0i[15:0] = y0_imag; y0r[15:0] = y0_real; y1i[15:0] = y1_imag; y1r[15:0] = y1_real;
  //   y2i[15:0] = y2_imag; y2r[15:0] = y2_real; y3i[15:0] = y3_imag; y3r[15:0] = y3_real; y4i[15:0] = y4_imag;
  //   y4r[15:0] = y4_real; y5i[15:0] = y5_imag; y5r[15:0] = y5_real; y6i[15:0] = y6_imag; y6r[15:0] = y6_real;
  //   y7i[15:0] = y7_imag; y7r[15:0] = y7_real; y8i[15:0] = y8_imag; y8r[15:0] = y8_real; y9i[15:0] = y9_imag;
  //   y9r[15:0] = y9_real; y10i[15:0] = y10_imag; y10r[15:0] = y10_real; y11i[15:0] = y11_imag; y11r[15:0] = y11_real;
  //   y12i[15:0] = y12_imag; y12r[15:0] = y12_real; y13i[15:0] = y13_imag; y13r[15:0] = y13_real;
  //   y14i[15:0] = y14_imag; y14r[15:0] = y14_real; y15i[15:0] = y15_imag; y15r[15:0] = y15_real

  // Notes on the sheet:
  //   Stage Three
  //   2 groups of size eight FFT
  //   mixing x_i with x_i+4
  //   each group consists of four butterfies
endmodule

module Stage_Four (
  input  [15:0] x0_real,
  input  [15:0] x0_imag,
  input  [15:0] x1_real,
  input  [15:0] x1_imag,
  input  [15:0] x2_real,
  input  [15:0] x2_imag,
  input  [15:0] x3_real,
  input  [15:0] x3_imag,
  input  [15:0] x4_real,
  input  [15:0] x4_imag,
  input  [15:0] x5_real,
  input  [15:0] x5_imag,
  input  [15:0] x6_real,
  input  [15:0] x6_imag,
  input  [15:0] x7_real,
  input  [15:0] x7_imag,
  input  [15:0] x8_real,
  input  [15:0] x8_imag,
  input  [15:0] x9_real,
  input  [15:0] x9_imag,
  input  [15:0] x10_real,
  input  [15:0] x10_imag,
  input  [15:0] x11_real,
  input  [15:0] x11_imag,
  input  [15:0] x12_real,
  input  [15:0] x12_imag,
  input  [15:0] x13_real,
  input  [15:0] x13_imag,
  input  [15:0] x14_real,
  input  [15:0] x14_imag,
  input  [15:0] x15_real,
  input  [15:0] x15_imag,
  output [15:0] y0_real,
  output [15:0] y0_imag,
  output [15:0] y1_real,
  output [15:0] y1_imag,
  output [15:0] y2_real,
  output [15:0] y2_imag,
  output [15:0] y3_real,
  output [15:0] y3_imag,
  output [15:0] y4_real,
  output [15:0] y4_imag,
  output [15:0] y5_real,
  output [15:0] y5_imag,
  output [15:0] y6_real,
  output [15:0] y6_imag,
  output [15:0] y7_real,
  output [15:0] y7_imag,
  output [15:0] y8_real,
  output [15:0] y8_imag,
  output [15:0] y9_real,
  output [15:0] y9_imag,
  output [15:0] y10_real,
  output [15:0] y10_imag,
  output [15:0] y11_real,
  output [15:0] y11_imag,
  output [15:0] y12_real,
  output [15:0] y12_imag,
  output [15:0] y13_real,
  output [15:0] y13_imag,
  output [15:0] y14_real,
  output [15:0] y14_imag,
  output [15:0] y15_real,
  output [15:0] y15_imag
);

  wire [15:0] mult_1_axb_imag, mult_1_axb_real, mult_2_axb_imag, mult_2_axb_real, mult_3_axb_imag,
       mult_3_axb_real, mult_4_axb_imag, mult_4_axb_real, mult_5_axb_imag, mult_5_axb_real, mult_6_axb_imag,
       mult_6_axb_real, negator_1_out;

  Mult mult_1 (
    .A_real(x9_real), .B_real(16'h7642), .A_imag(x9_imag), .B_imag(16'hcf04), .AxB_real(mult_1_axb_real),
    .AxB_imag(mult_1_axb_imag));
  Mult mult_2 (
    .A_real(x10_real), .B_real(16'h5a82), .A_imag(x10_imag), .B_imag(16'ha57e), .AxB_real(mult_2_axb_real),
    .AxB_imag(mult_2_axb_imag));
  Mult mult_3 (
    .A_real(x11_real), .B_real(16'h30fc), .A_imag(x11_imag), .B_imag(16'h89be), .AxB_real(mult_3_axb_real),
    .AxB_imag(mult_3_axb_imag));
  Negator #(.width(16)) negator_1 (.in(x12_real), .out(negator_1_out));
  Mult mult_4 (
    .A_real(x13_real), .B_real(16'hcf04), .A_imag(x13_imag), .B_imag(16'h89be), .AxB_real(mult_4_axb_real),
    .AxB_imag(mult_4_axb_imag));
  Mult mult_5 (
    .A_real(x14_real), .B_real(16'ha57e), .A_imag(x14_imag), .B_imag(16'ha57e), .AxB_real(mult_5_axb_real),
    .AxB_imag(mult_5_axb_imag));
  Mult mult_6 (
    .A_real(x15_real), .B_real(16'h89be), .A_imag(x15_imag), .B_imag(16'hcf04), .AxB_real(mult_6_axb_real),
    .AxB_imag(mult_6_axb_imag));
  Add_Sub_Shift add_sub_shift_1 (
    .X_real(x0_real), .X_imag(x0_imag), .Y_real(x8_real), .Y_imag(x8_imag), .Sum_Real(y0_real),
    .Sum_imag(y0_imag), .Dif_Real(y8_real), .Dif_imag(y8_imag));
  Add_Sub_Shift add_sub_shift_2 (
    .X_real(x1_real), .X_imag(x1_imag), .Y_real(mult_1_axb_real), .Y_imag(mult_1_axb_imag),
    .Sum_Real(y1_real), .Sum_imag(y1_imag), .Dif_Real(y9_real), .Dif_imag(y9_imag));
  Add_Sub_Shift add_sub_shift_3 (
    .X_real(x2_real), .X_imag(x2_imag), .Y_real(mult_2_axb_real), .Y_imag(mult_2_axb_imag),
    .Sum_Real(y2_real), .Sum_imag(y2_imag), .Dif_Real(y10_real), .Dif_imag(y10_imag));
  Add_Sub_Shift add_sub_shift_4 (
    .X_real(x3_real), .X_imag(x3_imag), .Y_real(mult_3_axb_real), .Y_imag(mult_3_axb_imag),
    .Sum_Real(y3_real), .Sum_imag(y3_imag), .Dif_Real(y11_real), .Dif_imag(y11_imag));
  Add_Sub_Shift add_sub_shift_5 (
    .X_real(x4_real), .X_imag(x4_imag), .Y_real(x12_imag), .Y_imag(negator_1_out), .Sum_Real(y4_real),
    .Sum_imag(y4_imag), .Dif_Real(y12_real), .Dif_imag(y12_imag));
  Add_Sub_Shift add_sub_shift_6 (
    .X_real(x5_real), .X_imag(x5_imag), .Y_real(mult_4_axb_real), .Y_imag(mult_4_axb_imag),
    .Sum_Real(y5_real), .Sum_imag(y5_imag), .Dif_Real(y13_real), .Dif_imag(y13_imag));
  Add_Sub_Shift add_sub_shift_7 (
    .X_real(x6_real), .X_imag(x6_imag), .Y_real(mult_5_axb_real), .Y_imag(mult_5_axb_imag),
    .Sum_Real(y6_real), .Sum_imag(y6_imag), .Dif_Real(y14_real), .Dif_imag(y14_imag));
  Add_Sub_Shift add_sub_shift_8 (
    .X_real(x7_real), .X_imag(x7_imag), .Y_real(mult_6_axb_real), .Y_imag(mult_6_axb_imag),
    .Sum_Real(y7_real), .Sum_imag(y7_imag), .Dif_Real(y15_real), .Dif_imag(y15_imag));

  // Other names for the same wires on the sheet: x0i[15:0] = x0_imag; x0r[15:0] = x0_real; x1i[15:0] = x1_imag;
  //   x1r[15:0] = x1_real; x2i[15:0] = x2_imag; x2r[15:0] = x2_real; x3i[15:0] = x3_imag; x3r[15:0] = x3_real;
  //   x4i[15:0] = x4_imag; x4r[15:0] = x4_real; x5i[15:0] = x5_imag; x5r[15:0] = x5_real; x6i[15:0] = x6_imag;
  //   x6r[15:0] = x6_real; x7i[15:0] = x7_imag; x7r[15:0] = x7_real; x8i[15:0] = x8_imag; x8r[15:0] = x8_real;
  //   x9i[15:0] = x9_imag; x9r[15:0] = x9_real; x10i[15:0] = x10_imag; x10r[15:0] = x10_real; x11i[15:0] = x11_imag;
  //   x11r[15:0] = x11_real; x12i[15:0] = x12_imag; x12r[15:0] = x12_real; x13i[15:0] = x13_imag;
  //   x13r[15:0] = x13_real; x14i[15:0] = x14_imag; x14r[15:0] = x14_real; x15i[15:0] = x15_imag;
  //   x15r[15:0] = x15_real; y0i[15:0] = y0_imag; y0r[15:0] = y0_real; y1i[15:0] = y1_imag; y1r[15:0] = y1_real;
  //   y2i[15:0] = y2_imag; y2r[15:0] = y2_real; y3i[15:0] = y3_imag; y3r[15:0] = y3_real; y4i[15:0] = y4_imag;
  //   y4r[15:0] = y4_real; y5i[15:0] = y5_imag; y5r[15:0] = y5_real; y6i[15:0] = y6_imag; y6r[15:0] = y6_real;
  //   y7i[15:0] = y7_imag; y7r[15:0] = y7_real; y8i[15:0] = y8_imag; y8r[15:0] = y8_real; y9i[15:0] = y9_imag;
  //   y9r[15:0] = y9_real; y10i[15:0] = y10_imag; y10r[15:0] = y10_real; y11i[15:0] = y11_imag; y11r[15:0] = y11_real;
  //   y12i[15:0] = y12_imag; y12r[15:0] = y12_real; y13i[15:0] = y13_imag; y13r[15:0] = y13_real;
  //   y14i[15:0] = y14_imag; y14r[15:0] = y14_real; y15i[15:0] = y15_imag; y15r[15:0] = y15_real

  // Notes on the sheet:
  //   Stage Four
  //   1 group of size sixteen FFT
  //   mixing x_i with x_i+8
  //   the group consists of 8 butterfies
endmodule
